// Logisim project ALU_A2_Group_2.circ as structural Verilog: 1 circuit, main circuit main
module main (
  input  Cs2,
  input  Cs1,
  input  Cs0,
  input  A3,
  input  A2,
  input  A1,
  input  A0,
  input  B3,
  input  B2,
  input  B1,
  input  B0,
  output C,
  output S,
  output V,
  output Z,
  output Cout,
  output F3,
  output F2,
  output F1,
  output F0
);

  wire n7404_1__2__1y, n7404_1__4__2y, n7404_1__6__3y, n7404_1__8__4y, n7404_1__12__6y, n7408_1__3__1y,
       n7408_1__6__2y, n7408_1__8__3y, n7408_1__11__4y, n7408_2__3__1y, n7432_1__3__1y, n7432_1__6__2y,
       n7432_1__8__3y, n7432_1__11__4y, n7432_2__3__1y, n7432_2__6__2y, n7432_2__11__4y, n7483_1__2__s3,
       n7483_1__6__s2, n7483_1__9__s1, n7483_1__15__s4, n7486_1__3__1y, n7486_1__6__2y, n7486_1__8__3y,
       n7486_1__11__4y, n7486_2__3__1y, n7486_2__6__2y, n7486_2__8__3y, n7486_2__11__4y, n7486_3__3__1y,
       n7486_3__6__2y, n7486_3__8__3y, n74157_1__4__y1, n74157_1__7__y2, n74157_1__9__y3, n74157_1__12__y4;

  _7486 u_7486_1 (
    ._1__1A(B3), ._2__1B(Cs2), ._3__1Y(n7486_1__3__1y), ._4__2A(B2), ._5__2B(Cs2), ._6__2Y(n7486_1__6__2y),
    ._7__GND(1'b0), ._14__Vcc(1'b1), ._13__4B(B0), ._12__4A(Cs2), ._11__4Y(n7486_1__11__4y), ._10__3B(B1),
    ._9__3A(Cs2), ._8__3Y(n7486_1__8__3y));
  _7486 u_7486_2 (
    ._1__1A(B3), ._2__1B(A3), ._3__1Y(n7486_2__3__1y), ._4__2A(B2), ._5__2B(A2), ._6__2Y(n7486_2__6__2y),
    ._14__Vcc(1'b1), ._13__4B(B0), ._12__4A(A0), ._11__4Y(n7486_2__11__4y), ._10__3B(B1), ._9__3A(A1),
    ._8__3Y(n7486_2__8__3y));  // open: _7__GND
  _7408 u_7408_1 (
    ._1__1A(A3), ._2__1B(B3), ._3__1Y(n7408_1__3__1y), ._4__2A(B2), ._5__2B(A2), ._6__2Y(n7408_1__6__2y),
    ._7__GND(1'b0), ._14__Vcc(1'b1), ._13__4B(B0), ._12__4A(A0), ._11__4Y(n7408_1__11__4y), ._10__3B(A1),
    ._9__3A(B1), ._8__3Y(n7408_1__8__3y));
  _7404 u_7404_1 (
    ._1__1A(n7486_1__3__1y), ._2__1Y(n7404_1__2__1y), ._3__2A(n7486_1__6__2y), ._4__2Y(n7404_1__4__2y),
    ._5__3A(n7486_1__8__3y), ._6__3Y(n7404_1__6__3y), ._7__GND(1'b0), ._14__Vcc(1'b1), ._13__6A(Cs1),
    ._12__6Y(n7404_1__12__6y), ._11__5A(n7432_2__6__2y), ._10__5Y(Z), ._9__4A(n7486_1__11__4y),
    ._8__4Y(n7404_1__8__4y));
  _7408 u_7408_2 (
    ._1__1A(Cs0), ._2__1B(Cs2), ._3__1Y(n7408_2__3__1y), ._7__GND(1'b0), ._14__Vcc(1'b1),
    ._13__4B(n7486_3__6__2y), ._12__4A(n7404_1__12__6y), ._11__4Y(V), ._10__3B(n7404_1__12__6y),
    ._9__3A(Cout), ._8__3Y(C));  // open: _4__2A, _5__2B, _6__2Y
  _74157 u_74157_1 (
    ._1__S(Cs0), ._2__A1(n7486_2__3__1y), ._3__B1(n7408_1__3__1y), ._4__Y1(n74157_1__4__y1),
    ._5__A2(n7486_2__6__2y), ._6__B2(n7408_1__6__2y), ._7__Y2(n74157_1__7__y2), ._8__GND(1'b0),
    ._16__Vcc(1'b1), ._15__G(1'b0), ._14__A4(n7486_2__11__4y), ._13__B4(n7408_1__11__4y),
    ._12__Y4(n74157_1__12__y4), ._11__A3(n7486_2__8__3y), ._10__B3(n7408_1__8__3y), ._9__Y3(n74157_1__9__y3));
  _7432 u_7432_1 (
    ._1__1A(n7404_1__2__1y), ._2__1B(n7408_2__3__1y), ._3__1Y(n7432_1__3__1y), ._4__2A(n7404_1__4__2y),
    ._5__2B(n7408_2__3__1y), ._6__2Y(n7432_1__6__2y), ._7__GND(1'b0), ._14__Vcc(1'b1),
    ._13__4B(n7408_2__3__1y), ._12__4A(n7404_1__8__4y), ._11__4Y(n7432_1__11__4y), ._10__3B(n7408_2__3__1y),
    ._9__3A(n7404_1__6__3y), ._8__3Y(n7432_1__8__3y));
  _7486 u_7486_3 (
    ._1__1A(A3), ._2__1B(n7432_1__3__1y), ._3__1Y(n7486_3__3__1y), ._4__2A(n7486_3__3__1y),
    ._5__2B(n7486_3__8__3y), ._6__2Y(n7486_3__6__2y), ._7__GND(1'b0), ._14__Vcc(1'b1),
    ._10__3B(n7483_1__15__s4), ._9__3A(Cout), ._8__3Y(n7486_3__8__3y));  // open: _13__4B, _12__4A, _11__4Y
  _7483 u_7483_1 (
    ._1__A4(A3), ._2__S3(n7483_1__2__s3), ._3__A3(A2), ._4__B3(n7432_1__6__2y), ._5__Vcc(1'b1),
    ._6__S2(n7483_1__6__s2), ._7__B2(n7432_1__8__3y), ._8__A2(A1), ._16__B4(n7432_1__3__1y),
    ._15__S4(n7483_1__15__s4), ._14__Cout(Cout), ._13__Cin(Cs0), ._12__GND(1'b0), ._11__B1(n7432_1__11__4y),
    ._10__A1(A0), ._9__S1(n7483_1__9__s1));
  _7432 u_7432_2 (
    ._1__1A(F3), ._2__1B(F2), ._3__1Y(n7432_2__3__1y), ._4__2A(n7432_2__3__1y), ._5__2B(n7432_2__11__4y),
    ._6__2Y(n7432_2__6__2y), ._7__GND(1'b0), ._14__Vcc(1'b1), ._13__4B(F1), ._12__4A(F0),
    ._11__4Y(n7432_2__11__4y));  // open: _10__3B, _9__3A, _8__3Y
  _74157 u_74157_2 (
    ._1__S(Cs1), ._2__A1(n7483_1__15__s4), ._3__B1(n74157_1__4__y1), ._4__Y1(F3), ._5__A2(n7483_1__2__s3),
    ._6__B2(n74157_1__7__y2), ._7__Y2(F2), ._8__GND(1'b0), ._16__Vcc(1'b1), ._15__G(1'b0),
    ._14__A4(n7483_1__9__s1), ._13__B4(n74157_1__12__y4), ._12__Y4(F0), ._11__A3(n7483_1__6__s2),
    ._10__B3(n74157_1__9__y3), ._9__Y3(F1));

  assign S = F3;

  // Notes on the sheet:
  //   FLAGS
  //   SELECT
  //   OUTPUT
  //   INPUT
  //   B3
  //   B2
  //   cs2 xor Bi
  //   XOR
  //   AND
  //   VCC
  //   B0
  //   B1
  //   cs2 xnor Bi
  //   cs2.cs0
  //   cs1'
  //   x3
  //   GND
  //   y3
  //   Yi
  //   s3
  //   Cout
  //   F3
  //   F1+F2+F3+F4
  //   VCC
  //   GND
endmodule
