// Logisim project ALU.circ as structural Verilog: 1 circuit, main circuit main
module main (
  input  cs2,
  input  cs1,
  input  cs0,
  input  A3,
  input  A2,
  input  A1,
  input  A0,
  input  B3,
  input  B2,
  input  B1,
  input  B0,
  output Cout,
  output F3,
  output F2,
  output F1,
  output F0,
  output S,
  output Z,
  output V,
  output C
);

  wire n7404_1_p1, n7404_1_p3, n7404_1_p5, n7404_1_p7, n7404_1_p9, n7404_1_p11, n7404_2_p1, n7404_2_p2,
       n7404_2_p3, n7404_2_p4, n7404_2_p5, n7404_2_p6, n7404_2_p7, n7404_2_p9, n7404_2_p10, n7404_2_p13,
       n7404_2_p14, n7404_2_p15, n7408_1_p1, n7408_1_p2, n7408_1_p3, n7408_1_p4, n7408_1_p5, n7408_1_p6,
       n7408_1_p7, n7408_1_p8, n7408_1_p9, n7408_1_p10, n7408_1_p11, n7408_1_p12, n7408_1_p13, n7408_1_p14,
       n7408_1_p15, n7408_1_p16, n7408_1_p17, n7408_2_p1, n7408_2_p3, n7408_2_p6, n7408_2_p9, n7408_2_p10,
       n7408_2_p12, n7408_2_p13, n7432_1_p1, n7432_1_p3, n7432_1_p4, n7432_1_p6, n7432_1_p7, n7432_1_p10,
       n7432_1_p12, n7432_1_p13, n7432_1_p15, n7432_1_p16, n7432_1_p17, n7432_1_p18, n7432_2_p3, n7432_2_p6,
       n7432_2_p8, n7432_2_p13, n7432_2_p14, n7432_2_p15, n7483_1_p1, n7483_1_p3, n7483_1_p4, n7483_1_p7,
       n7483_1_p9, n7483_1_p11, n7483_1_p12, n7483_1_p14, n7483_1_p15, n7483_1_p17, n7483_1_p18, n7486_1_p1,
       n7486_1_p2, n7486_1_p3, n7486_1_p4, n7486_1_p5, n7486_1_p6, n7486_1_p7, n7486_1_p8, n7486_1_p9,
       n7486_1_p10, n7486_1_p11, n7486_1_p12, n7486_1_p13, n7486_1_p14, n7486_1_p15, n7486_1_p16,
       n7486_1_p17, n7486_2__3__1y, n7486_2__6__2y, n7486_2__8__3y, n7486_2__11__4y, n74157_1_p1,
       n74157_1_p2, n74157_1_p5, n74157_1_p8, n74157_1_p14, n74157_1_p17, n74157_2_p1, n74157_2_p2,
       n74157_2_p5, n74157_2_p8, n74157_2_p10, n74157_2_p11, n74157_2_p14, n74157_2_p17, undriven,
       undriven_2, undriven_3, undriven_4, undriven_5, undriven_6, undriven_7, undriven_8, undriven_9;

  // _7486 7486_1: pin names not known; wires that end beside it: n7486_1_p1, n7486_1_p2, n7486_1_p3, n7486_1_p4, n7486_1_p5, n7486_1_p6, n7486_1_p7, n7486_1_p8, n7486_1_p9, n7486_1_p10, n7486_1_p11, n7486_1_p12, n7486_1_p13, n7486_1_p14, n7486_1_p15, n7486_1_p16, n7486_1_p17
  _7486 u_7486_2 (
    ._1__1A(A3), ._2__1B(undriven_2), ._3__1Y(n7486_2__3__1y), ._4__2A(undriven), ._5__2B(undriven_3),
    ._6__2Y(n7486_2__6__2y), ._7__GND(undriven_4), ._14__Vcc(n7486_1_p17), ._13__4B(undriven_7),
    ._12__4A(undriven_6), ._11__4Y(n7486_2__11__4y), ._10__3B(undriven_5), ._9__3A(A0),
    ._8__3Y(n7486_2__8__3y));
  // _7404 7404_1: pin names not known; wires that end beside it: n7404_1_p1, n7486_1_p4, n7404_1_p3, n7486_1_p7, n7404_1_p5, n7486_1_p1, n7404_1_p7, n7486_1_p13, n7404_1_p9, n7486_1_p16, n7404_1_p11
  // _7408 7408_1: pin names not known; wires that end beside it: n7408_1_p1, n7408_1_p2, n7408_1_p3, n7408_1_p4, n7408_1_p5, n7408_1_p6, n7408_1_p7, n7408_1_p8, n7408_1_p9, n7408_1_p10, n7408_1_p11, n7408_1_p12, n7408_1_p13, n7408_1_p14, n7408_1_p15, n7408_1_p16, n7408_1_p17
  // _7432 7432_1: pin names not known; wires that end beside it: n7432_1_p1, n7404_1_p3, n7432_1_p3, n7432_1_p4, n7404_1_p1, n7432_1_p6, n7432_1_p7, n7486_1_p1, n7486_1_p9, n7432_1_p10, n7404_1_p9, n7432_1_p12, n7432_1_p13, n7404_1_p11, n7432_1_p15, n7432_1_p16, n7432_1_p17, n7432_1_p18
  // _74157 74157_1: pin names not known; wires that end beside it: n74157_1_p1, n74157_1_p2, n7486_2__3__1y, n7408_1_p1, n74157_1_p5, n7486_2__6__2y, n7408_1_p2, n74157_1_p8, n7408_1_p10, n7486_1_p9, n7432_1_p17, n7486_2__11__4y, n7408_1_p14, n74157_1_p14, n7486_2__8__3y, n7408_1_p17, n74157_1_p17
  // _7483 7483_1: pin names not known; wires that end beside it: n7483_1_p1, A3, n7483_1_p3, n7483_1_p4, n7432_1_p1, n7432_1_p18, n7483_1_p7, n7432_1_p12, n7483_1_p9, n7432_1_p4, n7483_1_p11, n7483_1_p12, Cout, n7483_1_p14, n7483_1_p15, n7432_1_p16, n7483_1_p17, n7483_1_p18, n7486_1_p1
  // _74157 74157_2: pin names not known; wires that end beside it: n74157_2_p1, n74157_2_p2, n7483_1_p12, n74157_1_p5, n74157_2_p5, n7483_1_p3, n74157_1_p1, n74157_2_p8, n7483_1_p15, n74157_2_p10, n74157_2_p11, n7483_1_p7, n74157_1_p14, n74157_2_p14, n7483_1_p18, n74157_1_p17, n74157_2_p17
  // _7404 7404_2: pin names not known; wires that end beside it: n7404_2_p1, n7404_2_p2, n7404_2_p3, n7404_2_p4, n7404_2_p5, n7404_2_p6, n7404_2_p7, n74157_2_p1, n7404_2_p9, n7404_2_p10, Z, n7483_1_p11, n7404_2_p13, n7404_2_p14, n7404_2_p15
  // _7432 7432_2: pin names not known; wires that end beside it: n74157_2_p5, n74157_2_p8, n7432_2_p3, n74157_2_p14, F0, n7432_2_p6, n7404_2_p1, n7432_2_p8, n7404_2_p14, n7432_2_p6, n7432_2_p3, n7404_2_p10, n7432_2_p13, n7432_2_p14, n7432_2_p15
  // _7408 7408_2: pin names not known; wires that end beside it: n7408_2_p1, n7404_2_p15, n7408_2_p3, n7404_2_p7, n7404_2_p13, n7408_2_p6, n74157_2_p1, n7483_1_p1, n7408_2_p9, n7408_2_p10, n7432_1_p6, n7408_2_p12, n7408_2_p13, C, n7404_2_p3
  _7408 u_7408_3 (
    ._1__1A(n7408_2_p3), ._2__1B(n7404_2_p5), ._3__1Y(n7432_2_p14), ._4__2A(n7408_2_p6), ._5__2B(undriven_9),
    ._6__2Y(n7432_2_p13), ._7__GND(undriven_8), ._14__Vcc(n7432_2_p8), ._10__3B(n7432_2_p15),
    ._9__3A(n7408_2_p12), ._8__3Y(V));  // open: _13__4B, _12__4A, _11__4Y

  // Notes on the sheet:
  //   XNOR: cs2 xor Bi
  //   XOR unit
  //   invert
  //   AND unit
  //   Y = XNOR + cs2.cs0
  //   74157 logic mux (cs0)
  //   7483 adder
  //   74157 out mux (cs1)
  //   7404 flags
  //   7432 Z, V
  //   7408 C, k
  //   7408 V
endmodule
