// Logisim project submission.circ as structural Verilog: 1 circuit, main circuit main
module main (
  input  cs2,
  input  cs1,
  input  cs0,
  input  A3,
  input  A2,
  input  A1,
  input  A0,
  input  B3,
  input  B2,
  input  B1,
  input  B0,
  output Cout,
  output F3,
  output F2,
  output F1,
  output F0,
  output S,
  output Z,
  output V,
  output C
);

  wire n7408_1__3__1y, n7408_1__6__2y, n7408_1__8__3y, n7408_1__11__4y, n7408_2__11__4y, n7432_1__3__1y,
       n7432_1__6__2y, n7432_1__8__3y, n7432_1__11__4y, n7432_2__3__1y, n7432_2__6__2y, n7432_2__8__3y,
       n7432_2__11__4y, n7486_1__3__1y, n7486_1__6__2y, n7486_1__8__3y, n7486_1__11__4y, n7486_2__3__1y,
       n7486_2__6__2y, n7486_2__8__3y, n7486_2__11__4y, n7486_3__3__1y, n7486_3__6__2y, n7486_3__11__4y,
       n74153_1__7__y1, n74153_1__9__y2, n74153_2__7__y1, n74153_2__9__y2, n74157_1__4__y1, n74157_1__7__y2,
       n74157_1__9__y3, n74157_1__12__y4;

  _7408 u_7408_1 (
    ._1__1A(A3), ._2__1B(B3), ._3__1Y(n7408_1__3__1y), ._4__2A(A2), ._5__2B(B2), ._6__2Y(n7408_1__6__2y),
    ._7__GND(1'b0), ._14__Vcc(1'b1), ._13__4B(A1), ._12__4A(B1), ._11__4Y(n7408_1__11__4y), ._10__3B(A0),
    ._9__3A(B0), ._8__3Y(n7408_1__8__3y));
  _7432 u_7432_1 (
    ._1__1A(A3), ._2__1B(B3), ._3__1Y(n7432_1__3__1y), ._4__2A(A2), ._5__2B(B2), ._6__2Y(n7432_1__6__2y),
    ._7__GND(1'b0), ._14__Vcc(1'b1), ._13__4B(A1), ._12__4A(B1), ._11__4Y(n7432_1__11__4y), ._10__3B(A0),
    ._9__3A(B0), ._8__3Y(n7432_1__8__3y));
  _7486 u_7486_1 (
    ._1__1A(n7486_2__3__1y), ._2__1B(B3), ._3__1Y(n7486_1__3__1y), ._4__2A(n7486_2__3__1y), ._5__2B(B2),
    ._6__2Y(n7486_1__6__2y), ._7__GND(1'b0), ._14__Vcc(1'b1), ._13__4B(n7486_2__3__1y), ._12__4A(B1),
    ._11__4Y(n7486_1__11__4y), ._10__3B(n7486_2__3__1y), ._9__3A(B0), ._8__3Y(n7486_1__8__3y));
  _7486 u_7486_2 (
    ._1__1A(1'b1), ._2__1B(cs0), ._3__1Y(n7486_2__3__1y), ._4__2A(cs0), ._5__2B(cs1),
    ._6__2Y(n7486_2__6__2y), ._7__GND(1'b0), ._14__Vcc(1'b1), ._13__4B(n7486_2__3__1y), ._12__4A(cs1),
    ._11__4Y(n7486_2__11__4y), ._10__3B(cs2), ._9__3A(cs1), ._8__3Y(n7486_2__8__3y));
  _74153 u_74153_1 (
    ._1__nG1(1'b0), ._2__B(cs1), ._3__1C3(A3), ._4__1C2(n7432_1__3__1y), ._5__1C1(n7408_1__3__1y),
    ._6__1C0(A3), ._7__Y1(n74153_1__7__y1), ._8__GND(1'b0), ._16__Vcc(1'b1), ._15__nG2(1'b0), ._14__A(cs0),
    ._13__2C3(A2), ._12__2C2(n7432_1__6__2y), ._11__2C1(n7408_1__6__2y), ._10__2C0(A2),
    ._9__Y2(n74153_1__9__y2));
  _74153 u_74153_2 (
    ._1__nG1(1'b0), ._2__B(cs1), ._3__1C3(A1), ._4__1C2(n7432_1__11__4y), ._5__1C1(n7408_1__11__4y),
    ._6__1C0(A1), ._7__Y1(n74153_2__7__y1), ._8__GND(1'b0), ._16__Vcc(1'b1), ._15__nG2(1'b0), ._14__A(cs0),
    ._13__2C3(A0), ._12__2C2(n7432_1__8__3y), ._11__2C1(n7408_1__8__3y), ._10__2C0(A0),
    ._9__Y2(n74153_2__9__y2));
  _74157 u_74157_1 (
    ._1__S(n7486_2__8__3y), ._2__A1(n7486_1__3__1y), ._3__B1(cs0), ._4__Y1(n74157_1__4__y1),
    ._5__A2(n7486_1__6__2y), ._6__B2(cs0), ._7__Y2(n74157_1__7__y2), ._8__GND(1'b0), ._16__Vcc(1'b1),
    ._15__G(n7486_2__6__2y), ._14__A4(n7486_1__11__4y), ._13__B4(cs0), ._12__Y4(n74157_1__12__y4),
    ._11__A3(n7486_1__8__3y), ._10__B3(cs0), ._9__Y3(n74157_1__9__y3));
  // Probe on n74153_1__7__y1
  // Probe on n74153_1__9__y2
  // Probe on n74153_2__7__y1
  // Probe on n74153_2__9__y2
  // Probe on n74157_1__4__y1
  // Probe on n74157_1__7__y2
  // Probe on n74157_1__12__y4
  // Probe on n74157_1__9__y3
  // Probe on n7486_2__3__1y
  // Probe on n7486_2__11__4y
  _7483 u_7483_1 (
    ._1__A4(n74153_1__7__y1), ._2__S3(F2), ._3__A3(n74153_1__9__y2), ._4__B3(n74157_1__7__y2),
    ._5__Vcc(1'b1), ._6__S2(F1), ._7__B2(n74157_1__12__y4), ._8__A2(n74153_2__7__y1),
    ._16__B4(n74157_1__4__y1), ._15__S4(F3), ._14__Cout(Cout), ._13__Cin(n7408_2__11__4y), ._12__GND(1'b0),
    ._11__B1(n74157_1__9__y3), ._10__A1(n74153_2__9__y2), ._9__S1(F0));
  _7486 u_7486_3 (
    ._1__1A(n74153_1__7__y1), ._2__1B(n74157_1__4__y1), ._3__1Y(n7486_3__3__1y), ._4__2A(n7486_3__3__1y),
    ._5__2B(n7486_3__11__4y), ._6__2Y(n7486_3__6__2y), ._7__GND(1'b0), ._14__Vcc(1'b1), ._13__4B(F3),
    ._12__4A(Cout), ._11__4Y(n7486_3__11__4y), ._10__3B(1'b1), ._9__3A(n7432_2__8__3y), ._8__3Y(Z));
  _7408 u_7408_2 (
    ._1__1A(n7486_3__6__2y), ._2__1B(n7486_2__11__4y), ._3__1Y(V), ._4__2A(Cout), ._5__2B(n7486_2__11__4y),
    ._6__2Y(C), ._7__GND(1'b0), ._14__Vcc(1'b1), ._13__4B(n7486_2__11__4y), ._12__4A(n7432_2__6__2y),
    ._11__4Y(n7408_2__11__4y));  // open: _10__3B, _9__3A, _8__3Y
  _7432 u_7432_2 (
    ._1__1A(F2), ._2__1B(F3), ._3__1Y(n7432_2__3__1y), ._4__2A(n7486_2__3__1y), ._5__2B(cs2),
    ._6__2Y(n7432_2__6__2y), ._7__GND(1'b0), ._14__Vcc(1'b1), ._13__4B(F1), ._12__4A(F0),
    ._11__4Y(n7432_2__11__4y), ._10__3B(n7432_2__11__4y), ._9__3A(n7432_2__3__1y), ._8__3Y(n7432_2__8__3y));

  assign S = F3;
endmodule
