// Logisim project FPA -2.circ as structural Verilog: 17 circuits, main circuit main
module main (
  input  [15:0] in_1,
  output [15:0] out_2
);

  wire and_1_out, comparator_1_eq, comparator_1_gt, or_1_out;
  wire [3:1] undriven_2;
  wire [11:2] undriven;
  wire [11:11] adder_1_out;

  Comparator #(.width(4)) comparator_1 (
    .a({undriven_2, in_1[7]}), .b(4'b1000), .gt(comparator_1_gt), .eq(comparator_1_eq));  // open: lt
  Adder #(.width(12)) adder_1 (
    .a({undriven, in_1[9], in_1[11]}), .b({12{1'b0}}), .out({adder_1_out[11], out_2[15:5]}), .cin(or_1_out));  // open: cout
  and and_1 (and_1_out, in_1[11], comparator_1_eq);
  or or_1 (or_1_out, and_1_out, in_1[6], comparator_1_gt);
  // Pins of 1 and 12 bits meet at {undriven, in_1[9], in_1[11]}
  // Pins of 1 and 11 bits meet at {undriven, in_1[9]}
  // Pins of 1 and 4 bits meet at {undriven_2, in_1[7]}

  assign {in_1[8], in_1[5:0]} = {in_1[11], {6{in_1[6]}}};
  assign out_2[4:0] = {5{1'b0}};
endmodule

module a_unpacker (
  input  [15:0] \packed ,
  output Sign,
  output [3:0] Exponent,
  output [15:0] Fraction
);


  assign Exponent = \packed [14:11];
  assign Fraction = {\packed [10:0], {5{1'b0}}};
  assign Sign = \packed [15];
endmodule

module b_packer (
  input  Sign,
  input  [3:0] Exponent,
  input  [15:0] Fraction,
  output [15:0] \packed 
);


  assign \packed  = {Sign, Exponent, Fraction[15:5]};
endmodule

module c_Exponent_Differentiator (
  input  [3:0] Ea,
  input  [3:0] Eb,
  input  Sa,
  input  Sb,
  output Ea___Eb,
  output [3:0] Ea___Eb_2,
  output [3:0] max_Ea__Eb,
  output Max_sign,
  output Min_sign
);

  wire [3:0] multiplexer_1_out;
  wire [4:4] subtractor_1_out;

  Comparator #(.width(4), .mode("unsigned")) comparator_1 (.a(Ea), .b(Eb), .gt(Ea___Eb));  // open: eq, lt
  Multiplexer #(.width(4), .disabled(0)) multiplexer_1 (
    .in0(Ea), .in1(Eb), .out(multiplexer_1_out), .sel(Ea___Eb), .en(1'b1));
  Multiplexer #(.width(4), .disabled(0)) multiplexer_2 (.in0(Eb), .in1(Ea), .out(max_Ea__Eb), .sel(Ea___Eb), .en(1'b1));
  Subtractor #(.width(5)) subtractor_1 (
    .a({1'b0, max_Ea__Eb}), .b({1'b0, multiplexer_1_out}), .out({subtractor_1_out[4], Ea___Eb_2}), .bin(1'b0));  // open: bout
  Multiplexer #(.disabled(0)) multiplexer_3 (.in0(Sb), .in1(Sa), .out(Max_sign), .sel(Ea___Eb), .en(1'b1));
  Multiplexer #(.disabled(0)) multiplexer_4 (.in0(Sa), .in1(Sb), .out(Min_sign), .sel(Ea___Eb), .en(1'b1));
endmodule

module d_input_handler (
  input  [15:0] A,
  input  [15:0] B,
  output [15:0] larger_s_frac,
  output [15:0] Smaller_s_shifted_fract,
  output [15:0] smaller_s_frac,
  output [3:0] larger_s_exp,
  output [3:0] exp_diff,
  output smaller_s_sign,
  output larger_s_sign
);

  wire c_exponent_differentiator_1_ea___eb, unpacker_2_sign, unpacker_sign;
  wire [3:0] unpacker_2_exponent, unpacker_exponent;
  wire [15:0] unpacker_2_fraction, unpacker_fraction;

  a_unpacker unpacker (.\packed (A), .Sign(unpacker_sign), .Exponent(unpacker_exponent), .Fraction(unpacker_fraction));
  a_unpacker unpacker_2 (
    .\packed (B), .Sign(unpacker_2_sign), .Exponent(unpacker_2_exponent), .Fraction(unpacker_2_fraction));
  c_Exponent_Differentiator c_exponent_differentiator_1 (
    .Ea(unpacker_exponent), .Eb(unpacker_2_exponent), .Sa(unpacker_sign), .Sb(unpacker_2_sign),
    .Ea___Eb(c_exponent_differentiator_1_ea___eb), .Ea___Eb_2(exp_diff), .max_Ea__Eb(larger_s_exp),
    .Max_sign(larger_s_sign), .Min_sign(smaller_s_sign));
  Multiplexer #(.width(16)) multiplexer_1 (
    .in0(unpacker_2_fraction), .in1(unpacker_fraction), .out(larger_s_frac),
    .sel(c_exponent_differentiator_1_ea___eb), .en(1'b1));
  Multiplexer #(.width(16)) multiplexer_2 (
    .in0(unpacker_fraction), .in1(unpacker_2_fraction), .out(smaller_s_frac),
    .sel(c_exponent_differentiator_1_ea___eb), .en(1'b1));
  arbitraryRS arb_RS (.Input(smaller_s_frac), .Output(Smaller_s_shifted_fract), .Shift_amount(exp_diff));
endmodule

module e_adder_subtractor (
  input  [15:0] A,
  input  [15:0] B,
  input  Sa,
  input  Sb,
  output Cout,
  output [15:0] Sum
);

  wire xor_1_out;
  wire [15:0] adder_1_out, subtractor_1_out;

  Adder #(.width(16)) adder_1 (.a(A), .b(B), .out(adder_1_out), .cout(Cout));  // open: cin
  Subtractor #(.width(16)) subtractor_1 (.a(A), .b(B), .out(subtractor_1_out));  // open: bin, bout
  xor xor_1 (xor_1_out, Sa, Sb);
  Multiplexer #(.width(16)) multiplexer_1 (
    .in0(adder_1_out), .in1(subtractor_1_out), .out(Sum), .sel(xor_1_out), .en(1'b1));
endmodule

module _1brs (
  input  [15:0] in_1,
  input  in_2,
  output [15:0] out_3
);

  Multiplexer #(.width(16)) multiplexer_1 (.in0(in_1), .in1({1'b0, in_1[15:1]}), .out(out_3), .sel(in_2), .en(1'b1));
endmodule

module _2brs (
  input  [15:0] in_1,
  input  in_2,
  output [15:0] out_3
);

  Multiplexer #(.width(16)) multiplexer_1 (.in0(in_1), .in1({2'b00, in_1[15:2]}), .out(out_3), .sel(in_2), .en(1'b1));
endmodule

module _4brs (
  input  [15:0] in_1,
  input  in_2,
  output [15:0] out_3
);

  Multiplexer #(.width(16)) multiplexer_1 (.in0(in_1), .in1({4'b0000, in_1[15:4]}), .out(out_3), .sel(in_2), .en(1'b1));
endmodule

module _8brs (
  input  [15:0] in_1,
  input  in_2,
  output [15:0] out_3
);

  Multiplexer #(.width(16)) multiplexer_1 (
    .in0(in_1), .in1({{8{1'b0}}, in_1[15:8]}), .out(out_3), .sel(in_2), .en(1'b1));
endmodule

module arbitraryRS (
  input  [15:0] Input,
  input  [3:0] Shift_amount,
  output [15:0] Output
);

  wire [15:0] _1brs_out_3, _2brs_out_3, _4brs_out_3;

  _1brs _1brs (.in_1(Input), .in_2(Shift_amount[0]), .out_3(_1brs_out_3));
  _2brs _2brs (.in_1(_1brs_out_3), .in_2(Shift_amount[1]), .out_3(_2brs_out_3));
  _4brs _4brs (.in_1(_2brs_out_3), .in_2(Shift_amount[2]), .out_3(_4brs_out_3));
  _8brs _8brs (.in_1(_4brs_out_3), .in_2(Shift_amount[3]), .out_3(Output));
endmodule

module _1bls (
  input  [15:0] F,
  input  in_2,
  output [15:0] out_3
);

  Multiplexer #(.width(16)) multiplexer_1 (.in0(F), .in1({F[14:0], 1'b0}), .out(out_3), .sel(in_2), .en(1'b1));
endmodule

module _2bls (
  input  [15:0] F,
  input  S,
  output [15:0] out_3
);

  Multiplexer #(.width(16)) multiplexer_1 (.in0(F), .in1({F[13:0], 2'b00}), .out(out_3), .sel(S), .en(1'b1));
endmodule

module _4bls (
  input  [15:0] in_1,
  input  in_2,
  output [15:0] out_3
);

  Multiplexer #(.width(16)) multiplexer_1 (.in0(in_1), .in1({in_1[11:0], 4'b0000}), .out(out_3), .sel(in_2), .en(1'b1));
endmodule

module _8bls (
  input  [15:0] in_1,
  input  in_2,
  output [15:0] out_3
);

  Multiplexer #(.width(16)) multiplexer_1 (
    .in0(in_1), .in1({in_1[7:0], {8{1'b0}}}), .out(out_3), .sel(in_2), .en(1'b1));
endmodule

module arbitraryLS (
  input  [15:0] in_1,
  input  [3:0] in_2,
  output [15:0] out_3
);

  wire [15:0] n1bls_1_out_3, n2bls_1_out_3, n4bls_1_out_3;

  _1bls u_1bls_1 (.out_3(n1bls_1_out_3), .F(in_1), .in_2(in_2[0]));
  _2bls u_2bls_1 (.F(n1bls_1_out_3), .S(in_2[1]), .out_3(n2bls_1_out_3));
  _4bls u_4bls_1 (.in_1(n2bls_1_out_3), .in_2(in_2[2]), .out_3(n4bls_1_out_3));
  _8bls u_8bls_1 (.in_1(n4bls_1_out_3), .in_2(in_2[3]), .out_3(out_3));
endmodule

module rounder (
  input  [15:0] in_1,
  output [15:0] out_2
);

  wire adder_1_cout, and_1_out, or_1_out, or_2_out;

  or or_1 (or_1_out, in_1[0], in_1[1], in_1[2]);
  or or_2 (or_2_out, or_1_out, in_1[3], in_1[5]);
  and and_1 (and_1_out, or_2_out, in_1[4]);
  Adder #(.width(11)) adder_1 (.a(in_1[15:5]), .b({11{1'b0}}), .out(out_2[15:5]), .cin(and_1_out), .cout(adder_1_cout));

  assign out_2[4:0] = {5{1'b0}};
endmodule
