// Logisim project 1bitleftShifter.circ as structural Verilog: 1 circuit, main circuit main
module main (
  input  [15:0] F,
  input  in_2,
  output [15:0] out_3
);

  Multiplexer #(.width(16)) multiplexer_1 (.in0(F), .in1({F[14:0], 1'b0}), .out(out_3), .sel(in_2), .en(1'b1));
endmodule
