// Logisim project 2bitleftShifter.circ as structural Verilog: 1 circuit, main circuit main
module main (
  input  [15:0] F,
  input  S,
  output [15:0] out_3
);

  Multiplexer #(.width(16)) multiplexer_1 (.in0(F), .in1({F[13:0], 2'b00}), .out(out_3), .sel(S), .en(1'b1));
endmodule
