// Logisim project 8bitrightshifter.circ as structural Verilog: 1 circuit, main circuit main
module main (
  input  [15:0] in_1,
  input  in_2,
  output [15:0] out_3
);

  Multiplexer #(.width(16)) multiplexer_1 (
    .in0(in_1), .in1({{8{1'b0}}, in_1[15:8]}), .out(out_3), .sel(in_2), .en(1'b1));
endmodule
