// Logisim project ArbitraryLeftShifter.circ as structural Verilog: 1 circuit, main circuit main
module main (
  input  [15:0] in_1,
  input  [3:0] in_2,
  output [15:0] out_3
);

  wire [15:0] _1_out_3, _2_out_3, _4_out_3;

  _1bitleftShifter_main _1 (.out_3(_1_out_3), .F(in_1), .in_2(in_2[0]));
  _2bitleftShifter_main _2 (.F(_1_out_3), .S(in_2[1]), .out_3(_2_out_3));
  _4bitleftshifter_main _4 (.in_1(_2_out_3), .in_2(in_2[2]), .out_3(_4_out_3));
  _8bitleftshifter_main main_1 (.in_1(_4_out_3), .in_2(in_2[3]), .out_3(out_3));
endmodule
