// Logisim project ArbitraryRightShifter.circ as structural Verilog: 1 circuit, main circuit main
module main (
  input  [15:0] Input,
  input  [3:0] Shift_amount,
  output [15:0] Output
);

  wire [15:0] _1_out_3, _2_out_3, _4_out_3;

  _1bitrightshifter_main _1 (.in_1(Input), .in_2(Shift_amount[0]), .out_3(_1_out_3));
  _2bitrightshifter_main _2 (.in_1(_1_out_3), .in_2(Shift_amount[1]), .out_3(_2_out_3));
  _4bitrightshifter_main _4 (.in_1(_2_out_3), .in_2(Shift_amount[2]), .out_3(_4_out_3));
  _8bitrightshifter_main _8 (.in_1(_4_out_3), .in_2(Shift_amount[3]), .out_3(Output));
endmodule
