// Logisim project Shifters.circ as structural Verilog: 11 circuits, main circuit 1LS
// 1
module _1LS (
  input  [15:0] F,
  input  in_2,
  output [15:0] out_3
);

  Multiplexer #(.width(16)) multiplexer_1 (.in0(F), .in1({F[14:0], 1'b0}), .out(out_3), .sel(in_2), .en(1'b1));
endmodule

// 1
module _1RS (
  input  [15:0] in_1,
  input  in_2,
  output [15:0] out_3
);

  Multiplexer #(.width(16)) multiplexer_1 (.in0(in_1), .in1({1'b0, in_1[15:1]}), .out(out_3), .sel(in_2), .en(1'b1));
endmodule

// 2
module _2LS (
  input  [15:0] F,
  input  S,
  output [15:0] out_3
);

  Multiplexer #(.width(16)) multiplexer_1 (.in0(F), .in1({F[13:0], 2'b00}), .out(out_3), .sel(S), .en(1'b1));
endmodule

// 2
module _2RS (
  input  [15:0] in_1,
  input  in_2,
  output [15:0] out_3
);

  Multiplexer #(.width(16)) multiplexer_1 (.in0(in_1), .in1({2'b00, in_1[15:2]}), .out(out_3), .sel(in_2), .en(1'b1));
endmodule

// 4
module _4LS (
  input  [15:0] in_1,
  input  in_2,
  output [15:0] out_3
);

  Multiplexer #(.width(16)) multiplexer_1 (.in0(in_1), .in1({in_1[11:0], 4'b0000}), .out(out_3), .sel(in_2), .en(1'b1));
endmodule

// 4
module _4RS (
  input  [15:0] in_1,
  input  in_2,
  output [15:0] out_3
);

  Multiplexer #(.width(16)) multiplexer_1 (.in0(in_1), .in1({4'b0000, in_1[15:4]}), .out(out_3), .sel(in_2), .en(1'b1));
endmodule

// 8
module _8LS (
  input  [15:0] in_1,
  input  in_2,
  output [15:0] out_3
);

  Multiplexer #(.width(16)) multiplexer_1 (
    .in0(in_1), .in1({in_1[7:0], {8{1'b0}}}), .out(out_3), .sel(in_2), .en(1'b1));
endmodule

// 8
module _8RS (
  input  [15:0] in_1,
  input  in_2,
  output [15:0] out_3
);

  Multiplexer #(.width(16)) multiplexer_1 (
    .in0(in_1), .in1({{8{1'b0}}, in_1[15:8]}), .out(out_3), .sel(in_2), .en(1'b1));
endmodule

module ALS (
  input  [15:0] Input,
  input  [3:0] Shift_Amount,
  output [15:0] Output
);

  wire [15:0] n1ls_1_out_3, n2ls_1_out_3, n4ls_1_out_3;

  _1LS u_1ls_1 (.out_3(n1ls_1_out_3), .F(Input), .in_2(Shift_Amount[0]));
  _2LS u_2ls_1 (.F(n1ls_1_out_3), .S(Shift_Amount[1]), .out_3(n2ls_1_out_3));
  _4LS u_4ls_1 (.in_1(n2ls_1_out_3), .in_2(Shift_Amount[2]), .out_3(n4ls_1_out_3));
  _8LS u_8ls_1 (.in_1(n4ls_1_out_3), .in_2(Shift_Amount[3]), .out_3(Output));
endmodule

module ARS (
  input  [15:0] Input,
  input  [3:0] Shift_amount,
  output [15:0] Output
);

  wire [15:0] n1rs_1_out_3, n2rs_1_out_3, n4rs_1_out_3;

  _1RS u_1rs_1 (.in_1(Input), .in_2(Shift_amount[0]), .out_3(n1rs_1_out_3));
  _2RS u_2rs_1 (.in_1(n1rs_1_out_3), .in_2(Shift_amount[1]), .out_3(n2rs_1_out_3));
  _4RS u_4rs_1 (.in_1(n2rs_1_out_3), .in_2(Shift_amount[2]), .out_3(n4rs_1_out_3));
  _8RS u_8rs_1 (.in_1(n4rs_1_out_3), .in_2(Shift_amount[3]), .out_3(Output));
endmodule

module GS (
  input  [15:0] Input,
  input  [3:0] Shift_Amount,
  input  S,
  output [15:0] Output
);

  wire [15:0] als_1_output, ars_1_output;

  ARS ars_1 (.Input(Input), .Shift_amount(Shift_Amount), .Output(ars_1_output));
  ALS als_1 (.Input(Input), .Shift_Amount(Shift_Amount), .Output(als_1_output));
  Multiplexer #(.width(16), .disabled(0), .enable("false")) multiplexer_1 (
    .in0(ars_1_output), .in1(als_1_output), .out(Output), .sel(S));
endmodule
