// Logisim project mips_general.circ as structural Verilog: 7 circuits, main circuit main
module main (
  input  Reset,
  output [3:0] t0,
  output [3:0] t1,
  output [3:0] t2,
  output [3:0] t3,
  output [3:0] t4,
  output [3:0] sp
);

  wire ALU_zero_flag, Clock_out, Control_alusrc, Control_beq, Control_bneq, Control_jump, Control_memread,
       Control_memtoreg, Control_memwrite, Control_regdst, Control_regwrite, multiplexer_3_out;
  wire [2:0] Control_aluop;
  wire [3:0] ALU_output, Instruction__0_3, Instruction__4_7, Instruction__8_11, Instruction_opcode,
       Memory_data_read, multiplexer_1_out, multiplexer_2_out, multiplexer_6_out, Registers_readdata1,
       Registers_readdata2;
  wire [4:0] addres_maker_1_address_out;
  wire [7:0] adder_1_out, adder_2_out, bit_extender_1_out, Instruction_jmpaddr, Instruction_pc_read,
       multiplexer_4_out, multiplexer_5_out;

  // Probe on multiplexer_5_out
  Clock Clock (.out(Clock_out));
  // Probe on Instruction_pc_read
  Adder adder_1 (.a(Instruction_pc_read), .b(8'h1), .out(adder_1_out), .cin(1'b0));  // open: cout
  // Probe on Instruction_opcode
  Instruction Instruction (
    .PC_Write(multiplexer_5_out), .Clock(Clock_out), .Reset(Reset), .PC_Read(Instruction_pc_read),
    .Opcode(Instruction_opcode), ._8_11(Instruction__8_11), ._4_7(Instruction__4_7), ._0_3(Instruction__0_3),
    .JmpAddr(Instruction_jmpaddr));
  // Probe on Instruction__8_11
  // Probe on Instruction__4_7
  // Probe on Instruction__0_3
  Control Control (
    .OP_Code(Instruction_opcode), .ALUOp(Control_aluop), .Jump(Control_jump), .bneq(Control_bneq),
    .beq(Control_beq), .MemWrite(Control_memwrite), .MemRead(Control_memread), .RegWrite(Control_regwrite),
    .MemToReg(Control_memtoreg), .ALUSrc(Control_alusrc), .RegDst(Control_regdst));
  Multiplexer #(.width(4), .enable("false")) multiplexer_1 (
    .in0(Instruction__4_7), .in1(Instruction__0_3), .out(multiplexer_1_out), .sel(Control_regdst));
  // Probe on multiplexer_1_out
  Registers Registers (
    .DstReg1(multiplexer_1_out), .WriteData(multiplexer_6_out), .CLR(Reset), .SrcReg1(Instruction__8_11),
    .SrcReg2(Instruction__4_7), .ReadData1(Registers_readdata1), .ReadData2(Registers_readdata2),
    .RegWrite(Control_regwrite), .CLK(Clock_out), .sp__t4__t3__t2__t1__t0({sp, t4, t3, t2, t1, t0}));
  // Probe on Registers_readdata1
  assign bit_extender_1_out = {{4{Instruction__0_3[3]}}, Instruction__0_3};  // Bit_Extender bit_extender_1
  Multiplexer #(.width(4), .enable("false")) multiplexer_2 (
    .in0(Registers_readdata2), .in1(Instruction__0_3), .out(multiplexer_2_out), .sel(Control_alusrc));
  Adder adder_2 (.a(bit_extender_1_out), .b(adder_1_out), .out(adder_2_out), .cin(1'b0));  // open: cout
  _4bit_ALU ALU (
    .ALUOp(Control_aluop), .A(Registers_readdata1), .B(multiplexer_2_out), .Zero_Flag(ALU_zero_flag),
    .Output(ALU_output));
  // Probe on multiplexer_2_out
  Multiplexer #(.enable("false")) multiplexer_3 (
    .in0(Control_bneq), .in1(Control_beq), .out(multiplexer_3_out), .sel(ALU_zero_flag));
  // Probe on ALU_output
  // Probe on Registers_readdata2
  addres_maker addres_maker_1 (
    .address_in(ALU_output), .registor(Instruction__8_11), .address_out(addres_maker_1_address_out));
  Multiplexer #(.width(8), .enable("false")) multiplexer_4 (
    .in0(adder_1_out), .in1(adder_2_out), .out(multiplexer_4_out), .sel(multiplexer_3_out));
  Multiplexer #(.width(8), .enable("false")) multiplexer_5 (
    .in0(multiplexer_4_out), .in1(Instruction_jmpaddr), .out(multiplexer_5_out), .sel(Control_jump));
  Data_Memory Memory (
    .Address(addres_maker_1_address_out), .WriteData(Registers_readdata2), .CLK(Clock_out), .CLear(Reset),
    .MemRead(Control_memread), .MemWrite(Control_memwrite), .Data_Read(Memory_data_read));
  Multiplexer #(.width(4), .enable("false")) multiplexer_6 (
    .in0(ALU_output), .in1(Memory_data_read), .out(multiplexer_6_out), .sel(Control_memtoreg));

  // Notes on the sheet:
  //   address maker
  //   if $sp used, go to stack memory
endmodule

module Registers (
  input  RegWrite,
  input  CLK,
  input  [3:0] DstReg1,
  input  [3:0] WriteData,
  input  CLR,
  input  [3:0] SrcReg1,
  input  [3:0] SrcReg2,
  output [23:0] sp__t4__t3__t2__t1__t0,
  output [3:0] ReadData1,
  output [3:0] ReadData2
);

  wire and_1_out, demultiplexer_1_out1, demultiplexer_1_out2, demultiplexer_1_out3, demultiplexer_1_out4,
       demultiplexer_1_out5, demultiplexer_1_out6, not_1_out, not_2_out, not_3_out, not_4_out, not_5_out,
       not_6_out;

  not not_1 (not_1_out, demultiplexer_1_out2);
  not not_2 (not_2_out, demultiplexer_1_out3);
  Register #(.width(4)) t1 (.D(WriteData), .Q(sp__t4__t3__t2__t1__t0[7:4]), .clk(not_1_out), .clr(CLR));  // open: en
  Multiplexer #(.select(3), .width(4), .enable("false")) multiplexer_1 (
    .in0(4'b0000), .in1(sp__t4__t3__t2__t1__t0[3:0]), .in2(sp__t4__t3__t2__t1__t0[7:4]),
    .in3(sp__t4__t3__t2__t1__t0[11:8]), .in4(sp__t4__t3__t2__t1__t0[15:12]),
    .in5(sp__t4__t3__t2__t1__t0[19:16]), .in6(sp__t4__t3__t2__t1__t0[23:20]), .out(ReadData1),
    .sel(SrcReg1[2:0]));  // open: in7
  Demultiplexer #(.select(3), .enable("false")) demultiplexer_1 (
    .out1(demultiplexer_1_out1), .out2(demultiplexer_1_out2), .out3(demultiplexer_1_out3),
    .out4(demultiplexer_1_out4), .out5(demultiplexer_1_out5), .out6(demultiplexer_1_out6), .in(and_1_out),
    .sel(DstReg1[2:0]));  // open: out0, out7
  Register #(.width(4)) t2 (.D(WriteData), .Q(sp__t4__t3__t2__t1__t0[11:8]), .clk(not_2_out), .clr(CLR));  // open: en
  not not_3 (not_3_out, demultiplexer_1_out4);
  Register #(.width(4)) t3 (.D(WriteData), .Q(sp__t4__t3__t2__t1__t0[15:12]), .clk(not_3_out), .clr(CLR));  // open: en
  not not_4 (not_4_out, demultiplexer_1_out5);
  Register #(.width(4)) t4 (.D(WriteData), .Q(sp__t4__t3__t2__t1__t0[19:16]), .clk(not_4_out), .clr(CLR));  // open: en
  and and_1 (and_1_out, RegWrite, CLK);
  not not_5 (not_5_out, demultiplexer_1_out1);
  Register #(.width(4)) t0 (.D(WriteData), .Q(sp__t4__t3__t2__t1__t0[3:0]), .clk(not_5_out), .clr(CLR));  // open: en
  Multiplexer #(.select(3), .width(4), .enable("false")) multiplexer_2 (
    .in0(4'b0000), .in1(sp__t4__t3__t2__t1__t0[3:0]), .in2(sp__t4__t3__t2__t1__t0[7:4]),
    .in3(sp__t4__t3__t2__t1__t0[11:8]), .in4(sp__t4__t3__t2__t1__t0[15:12]),
    .in5(sp__t4__t3__t2__t1__t0[19:16]), .in6(sp__t4__t3__t2__t1__t0[23:20]), .out(ReadData2),
    .sel(SrcReg2[2:0]));  // open: in7
  not not_6 (not_6_out, demultiplexer_1_out6);
  Register #(.width(4)) sp (.D(WriteData), .Q(sp__t4__t3__t2__t1__t0[23:20]), .clk(not_6_out), .clr(CLR));  // open: en
endmodule

module _4bit_ALU (
  input  [2:0] ALUOp,
  input  [3:0] A,
  input  [3:0] B,
  output Zero_Flag,
  output [3:0] Output
);

  wire [3:0] adder_1_out, and_1_out, nor_1_out, or_1_out, shifter_1_out, shifter_2_out, subtractor_1_out;

  Adder #(.width(4)) adder_1 (.a(A), .b(B), .out(adder_1_out), .cin(1'b0));  // open: cout
  Subtractor #(.width(4)) subtractor_1 (.a(A), .b(B), .out(subtractor_1_out), .bin(1'b0));  // open: bout
  assign and_1_out = A & B;  // AND_Gate and_1, 4 bits wide
  assign or_1_out = A | B;  // OR_Gate or_1, 4 bits wide
  assign nor_1_out = ~(A | B);  // NOR_Gate nor_1, 4 bits wide
  Shifter #(.width(4)) shifter_1 (.in(A), .\dist (B[1:0]), .out(shifter_1_out));
  Shifter #(.width(4), .shift("lr")) shifter_2 (.in(A), .\dist (B[1:0]), .out(shifter_2_out));
  Multiplexer #(.select(3), .width(4), .enable("false")) multiplexer_1 (
    .in0(adder_1_out), .in1(subtractor_1_out), .in2(and_1_out), .in3(or_1_out), .in4(nor_1_out),
    .in5(shifter_1_out), .in6(shifter_2_out), .in7(4'b0000), .out(Output), .sel(ALUOp));
  nor nor_2 (Zero_Flag, Output[0], Output[1], Output[2], Output[3]);
endmodule

module Data_Memory (
  input  MemRead,
  input  MemWrite,
  input  [4:0] Address,
  input  [3:0] WriteData,
  input  CLK,
  input  CLear,
  output [3:0] Data_Read
);

  wire not_1_out;

  not not_1 (not_1_out, CLK);
  RAM #(.addrWidth(5), .dataWidth(4), .bus("separate")) ram_1 (
    .addr(Address), .din(WriteData), .data(Data_Read), .str(MemWrite), .clk(not_1_out), .ld(MemRead),
    .clr(CLear));  // open: sel
endmodule

module Instruction (
  input  [7:0] PC_Write,
  input  Clock,
  input  Reset,
  output [7:0] PC_Read,
  output [3:0] Opcode,
  output [3:0] _8_11,
  output [3:0] _4_7,
  output [3:0] _0_3,
  output [7:0] JmpAddr
);

  Register #(.trigger("falling")) PC (.D(PC_Write), .Q(PC_Read), .clk(Clock), .clr(Reset));  // open: en
  ROM #(.dataWidth(16)) rom_1 (.addr(PC_Read), .data({Opcode, _8_11, _4_7, _0_3}), .sel(1'b1));

  assign JmpAddr = {_8_11, _4_7};

  // Notes on the sheet:
  //   contents of rom_1 (hex, n*v repeats v):
  //   3113 3225 7661 2610 7661 2620 6114 4610 3661 4630 3661 d333
endmodule

module Control (
  input  [3:0] OP_Code,
  output [2:0] ALUOp,
  output Jump,
  output bneq,
  output beq,
  output MemWrite,
  output MemRead,
  output RegWrite,
  output MemToReg,
  output ALUSrc,
  output RegDst
);

  ROM #(.addrWidth(4), .dataWidth(12)) rom_1 (
    .addr(OP_Code), .data({RegDst, ALUSrc, MemToReg, RegWrite, MemRead, MemWrite, beq, bneq, Jump, ALUOp}));  // open: sel

  // Notes on the sheet:
  //   contents of rom_1 (hex, n*v repeats v):
  //   901 505 440 500 780 902 503 501 900 903 11 506 8 904 502 21
endmodule

module addres_maker (
  input  [3:0] address_in,
  input  [3:0] registor,
  output [4:0] address_out
);

  wire comparator_1_eq;
  wire [4:0] adder_1_out;

  Comparator #(.width(4), .mode("unsigned")) comparator_1 (
    .a(registor), .b(4'b0110), .eq(comparator_1_eq));  // open: gt, lt
  Adder #(.width(5)) adder_1 (.a({1'b0, address_in}), .b(5'b10000), .out(adder_1_out), .cin(1'b0));  // open: cout
  Multiplexer #(.width(5), .disabled(0), .enable("false")) multiplexer_1 (
    .in0({1'b0, address_in}), .in1(adder_1_out), .out(address_out), .sel(comparator_1_eq));
endmodule
