// Logisim project mips_pipelined.circ as structural Verilog: 9 circuits, main circuit Registers
module main (
  input  Reset
);

  wire _4bit_Alu_zero_flag, Clk_out, instruction_decode_1_stall, multiplexer_5_out, register_14_q;
  wire [3:0] _4bit_Alu_output, data_memory_1_data_read, instruction_decode_1__0_3, instruction_decode_1__4_7,
       instruction_decode_1__8_11, instruction_decode_1__12_15, multiplexer_2_out, multiplexer_3_out,
       multiplexer_7_out, register_5_q, register_6_q, register_7_q, register_8_q, register_11_q,
       register_12_q, register_13_q, register_15_q, register_16_q, registers_1_readdata1,
       registers_1_readdata2, registers_1_sp__t4__t3__t2__t1__t0, registers_1_sp__t4__t3__t2__t1__t0_3,
       registers_1_sp__t4__t3__t2__t1__t0_4, registers_1_sp__t4__t3__t2__t1__t0_5,
       registers_1_sp__t4__t3__t2__t1__t0_6;
  wire [7:0] adder_1_out, adder_2_out, bit_extender_1_out, instruction_1_pc_read,
       instruction_decode_1_jump_addr, multiplexer_1_out, multiplexer_4_out, multiplexer_6_out, register_1_q,
       register_4_q;
  wire [7:4] registers_1_sp__t4__t3__t2__t1__t0_2;
  wire [11:0] control_1_control_signals, register_3_q, register_9_q;
  wire [15:0] instruction_1_pc_out, register_2_q;

  Multiplexer #(.width(8), .disabled(0), .enable("false")) multiplexer_1 (
    .in0(adder_1_out), .in1(instruction_decode_1_jump_addr), .out(multiplexer_1_out),
    .sel(control_1_control_signals[3]));
  Adder adder_1 (.a(8'h1), .b(instruction_1_pc_read), .out(adder_1_out), .cin(1'b0));  // open: cout
  Instruction instruction_1 (
    .PC_Read(instruction_1_pc_read), .PC_Write(multiplexer_1_out), .PC_out(instruction_1_pc_out),
    .Clock(Clk_out), .Reset(Reset));
  Register register_1 (.D(adder_1_out), .Q(register_1_q), .clk(Clk_out), .clr(Reset));  // open: en
  Register #(.width(16)) register_2 (
    .D(instruction_1_pc_out), .Q(register_2_q), .clk(Clk_out), .clr(Reset));  // open: en
  Hex_Digit_Display hex_digit_display_1 (.value(registers_1_sp__t4__t3__t2__t1__t0_6));  // open: dp
  instruction_decode instruction_decode_1 (
    .instruction(register_2_q), .jump_addr(instruction_decode_1_jump_addr),
    .stall(instruction_decode_1_stall), ._12_15(instruction_decode_1__12_15),
    ._8_11(instruction_decode_1__8_11), ._4_7(instruction_decode_1__4_7), ._0_3(instruction_decode_1__0_3));
  Hex_Digit_Display hex_digit_display_2 (.value(registers_1_sp__t4__t3__t2__t1__t0_5));  // open: dp
  Hex_Digit_Display hex_digit_display_3 (.value(registers_1_sp__t4__t3__t2__t1__t0_4));  // open: dp
  Multiplexer #(.width(4), .disabled(0), .enable("false")) multiplexer_2 (
    .in0(instruction_decode_1__4_7), .in1(instruction_decode_1__0_3), .out(multiplexer_2_out),
    .sel(control_1_control_signals[11]));
  Hex_Digit_Display hex_digit_display_4 (.value(registers_1_sp__t4__t3__t2__t1__t0_3));  // open: dp
  Hex_Digit_Display hex_digit_display_5 (.value(registers_1_sp__t4__t3__t2__t1__t0_2));  // open: dp
  Control control_1 (.OP_Code(instruction_decode_1__12_15), .Control_Signals(control_1_control_signals));
  Hex_Digit_Display hex_digit_display_6 (.value(registers_1_sp__t4__t3__t2__t1__t0));  // open: dp
  Registers registers_1 (
    .DstReg1(register_16_q), .WriteData(register_15_q), .CLR(Reset), .SrcReg1(instruction_decode_1__8_11),
    .SrcReg2(instruction_decode_1__4_7), .ReadData1(registers_1_readdata1),
    .ReadData2(registers_1_readdata2), .RegWrite(register_14_q), .CLK(Clk_out),
    .sp__t4__t3__t2__t1__t0({registers_1_sp__t4__t3__t2__t1__t0_6, registers_1_sp__t4__t3__t2__t1__t0_5, registers_1_sp__t4__t3__t2__t1__t0_4, registers_1_sp__t4__t3__t2__t1__t0_3, registers_1_sp__t4__t3__t2__t1__t0_2, registers_1_sp__t4__t3__t2__t1__t0}));
  Register #(.width(12)) register_3 (
    .D(control_1_control_signals), .Q(register_3_q), .clk(Clk_out), .clr(Reset));  // open: en
  Register register_4 (.D(register_1_q), .Q(register_4_q), .clk(Clk_out), .clr(Reset));  // open: en
  Register #(.width(4)) register_5 (
    .D(registers_1_readdata1), .Q(register_5_q), .clk(Clk_out), .clr(Reset));  // open: en
  Register #(.width(4)) register_6 (
    .D(registers_1_readdata2), .Q(register_6_q), .clk(Clk_out), .clr(Reset));  // open: en
  Register #(.width(4)) register_7 (
    .D(instruction_decode_1__0_3), .Q(register_7_q), .clk(Clk_out), .clr(Reset));  // open: en
  Register #(.width(4)) register_8 (.D(multiplexer_2_out), .Q(register_8_q), .clk(Clk_out), .clr(Reset));  // open: en
  Multiplexer #(.width(4), .disabled(0), .enable("false")) multiplexer_3 (
    .in0(register_6_q), .in1(register_7_q), .out(multiplexer_3_out), .sel(register_3_q[10]));
  assign bit_extender_1_out = {{4{register_7_q[3]}}, register_7_q};  // Bit_Extender bit_extender_1
  Adder adder_2 (.a(register_4_q), .b(bit_extender_1_out), .out(adder_2_out), .cin(1'b0));  // open: cout
  _4bit_ALU _4bit_Alu (
    .ALUOp(register_3_q[2:0]), .A(register_5_q), .B(multiplexer_3_out), .Zero_Flag(_4bit_Alu_zero_flag),
    .Output(_4bit_Alu_output));
  Clock Clk (.out(Clk_out));
  Multiplexer #(.width(8), .disabled(0), .enable("false")) multiplexer_4 (
    .in0(register_4_q), .in1(adder_2_out), .out(multiplexer_4_out), .sel(multiplexer_5_out));
  Multiplexer #(.disabled(0), .enable("false")) multiplexer_5 (
    .in0(register_3_q[4]), .in1(register_3_q[5]), .out(multiplexer_5_out), .sel(_4bit_Alu_zero_flag));
  Multiplexer #(.width(8), .disabled(0), .enable("false")) multiplexer_6 (
    .in0(multiplexer_4_out), .in1(instruction_decode_1_jump_addr), .out(multiplexer_6_out),
    .sel(register_3_q[3]));
  Register #(.width(12)) register_9 (.D(register_3_q), .Q(register_9_q), .clk(Clk_out), .clr(Reset));  // open: en
  Register register_10 (.D(multiplexer_6_out), .clk(Clk_out), .clr(Reset));  // open: en, Q
  Register #(.width(4)) register_11 (.D(_4bit_Alu_output), .Q(register_11_q), .clk(Clk_out), .clr(Reset));  // open: en
  Register #(.width(4)) register_12 (.D(register_6_q), .Q(register_12_q), .clk(Clk_out), .clr(Reset));  // open: en
  Register #(.width(4)) register_13 (.D(register_8_q), .Q(register_13_q), .clk(Clk_out), .clr(Reset));  // open: en
  // Probe on register_9_q[7]
  // Probe on register_9_q[6]
  Data_Memory data_memory_1 (
    .Address(register_11_q), .WriteData(register_12_q), .CLK(Clk_out), .CLear(Reset),
    .MemRead(register_9_q[7]), .MemWrite(register_9_q[6]), .Data_Read(data_memory_1_data_read));
  Multiplexer #(.width(4), .disabled(0), .enable("false")) multiplexer_7 (
    .in0(register_11_q), .in1(data_memory_1_data_read), .out(multiplexer_7_out), .sel(register_9_q[9]));
  Register #(.width(1)) register_14 (.D(register_9_q[8]), .Q(register_14_q), .clk(Clk_out), .clr(Reset));  // open: en
  Register #(.width(4)) register_15 (.D(multiplexer_7_out), .Q(register_15_q), .clk(Clk_out), .clr(Reset));  // open: en
  Register #(.width(4)) register_16 (.D(register_13_q), .Q(register_16_q), .clk(Clk_out), .clr(Reset));  // open: en

  // Notes on the sheet:
  //   Instruction
  //   IF/ID
  //   decode
  //   sp
  //   Jump  Addr
  //   t4
  //   t3
  //   Control
  //   Reg Dst
  //   t2
  //   t1
  //   Registors
  //   t0
  //   Reg Write
  //   ID/EX
  //   Alu src
  //   Alu Op
  //   Alu Src
  //   beq
  //   bneq
  //   jump
  //   EX/MEM
  //   memory
  //   MEM/WB
endmodule

module Registers (
  input  RegWrite,
  input  CLK,
  input  [3:0] DstReg1,
  input  [3:0] WriteData,
  input  CLR,
  input  [3:0] SrcReg1,
  input  [3:0] SrcReg2,
  output [23:0] sp__t4__t3__t2__t1__t0,
  output [3:0] ReadData1,
  output [3:0] ReadData2
);

  wire and_1_out, demultiplexer_1_out1, demultiplexer_1_out2, demultiplexer_1_out3, demultiplexer_1_out4,
       demultiplexer_1_out5, demultiplexer_1_out6;

  Register #(.width(4)) t1 (
    .D(WriteData), .Q(sp__t4__t3__t2__t1__t0[7:4]), .clk(demultiplexer_1_out2), .clr(CLR));  // open: en
  Multiplexer #(.select(3), .width(4), .enable("false")) multiplexer_1 (
    .in0(4'b0000), .in1(sp__t4__t3__t2__t1__t0[3:0]), .in2(sp__t4__t3__t2__t1__t0[7:4]),
    .in3(sp__t4__t3__t2__t1__t0[11:8]), .in4(sp__t4__t3__t2__t1__t0[15:12]),
    .in5(sp__t4__t3__t2__t1__t0[19:16]), .in6(sp__t4__t3__t2__t1__t0[23:20]), .out(ReadData1),
    .sel(SrcReg1[2:0]));  // open: in7
  Demultiplexer #(.select(3), .enable("false")) demultiplexer_1 (
    .out1(demultiplexer_1_out1), .out2(demultiplexer_1_out2), .out3(demultiplexer_1_out3),
    .out4(demultiplexer_1_out4), .out5(demultiplexer_1_out5), .out6(demultiplexer_1_out6), .in(and_1_out),
    .sel(DstReg1[2:0]));  // open: out0, out7
  Register #(.width(4)) t2 (
    .D(WriteData), .Q(sp__t4__t3__t2__t1__t0[11:8]), .clk(demultiplexer_1_out3), .clr(CLR));  // open: en
  Register #(.width(4)) t3 (
    .D(WriteData), .Q(sp__t4__t3__t2__t1__t0[15:12]), .clk(demultiplexer_1_out4), .clr(CLR));  // open: en
  Register #(.width(4)) t4 (
    .D(WriteData), .Q(sp__t4__t3__t2__t1__t0[19:16]), .clk(demultiplexer_1_out5), .clr(CLR));  // open: en
  and and_1 (and_1_out, RegWrite, CLK);
  Register #(.width(4)) t0 (
    .D(WriteData), .Q(sp__t4__t3__t2__t1__t0[3:0]), .clk(demultiplexer_1_out1), .clr(CLR));  // open: en
  Multiplexer #(.select(3), .width(4), .enable("false")) multiplexer_2 (
    .in0(4'b0000), .in1(sp__t4__t3__t2__t1__t0[3:0]), .in2(sp__t4__t3__t2__t1__t0[7:4]),
    .in3(sp__t4__t3__t2__t1__t0[11:8]), .in4(sp__t4__t3__t2__t1__t0[15:12]),
    .in5(sp__t4__t3__t2__t1__t0[19:16]), .in6(sp__t4__t3__t2__t1__t0[23:20]), .out(ReadData2),
    .sel(SrcReg2[2:0]));  // open: in7
  Register #(.width(4)) sp (
    .D(WriteData), .Q(sp__t4__t3__t2__t1__t0[23:20]), .clk(demultiplexer_1_out6), .clr(CLR));  // open: en
endmodule

module _4bit_ALU (
  input  [2:0] ALUOp,
  input  [3:0] A,
  input  [3:0] B,
  output Zero_Flag,
  output [3:0] Output
);

  wire [3:0] adder_1_out, and_1_out, nor_1_out, or_1_out, shifter_1_out, shifter_2_out, subtractor_1_out;

  Adder #(.width(4)) adder_1 (.a(A), .b(B), .out(adder_1_out), .cin(1'b0));  // open: cout
  Subtractor #(.width(4)) subtractor_1 (.a(A), .b(B), .out(subtractor_1_out), .bin(1'b0));  // open: bout
  assign and_1_out = A & B;  // AND_Gate and_1, 4 bits wide
  assign or_1_out = A | B;  // OR_Gate or_1, 4 bits wide
  assign nor_1_out = ~(A | B);  // NOR_Gate nor_1, 4 bits wide
  Shifter #(.width(4)) shifter_1 (.in(A), .\dist (B[1:0]), .out(shifter_1_out));
  Shifter #(.width(4), .shift("lr")) shifter_2 (.in(A), .\dist (B[1:0]), .out(shifter_2_out));
  Multiplexer #(.select(3), .width(4), .enable("false")) multiplexer_1 (
    .in0(adder_1_out), .in1(subtractor_1_out), .in2(and_1_out), .in3(or_1_out), .in4(nor_1_out),
    .in5(shifter_1_out), .in6(shifter_2_out), .in7(4'b0000), .out(Output), .sel(ALUOp));
  nor nor_2 (Zero_Flag, Output[0], Output[1], Output[2], Output[3]);
endmodule

module Data_Memory (
  input  MemRead,
  input  MemWrite,
  input  [3:0] Address,
  input  [3:0] WriteData,
  input  CLK,
  input  CLear,
  output [3:0] Data_Read
);

  wire not_1_out;

  not not_1 (not_1_out, CLK);
  RAM #(.addrWidth(4), .dataWidth(4), .bus("separate")) ram_1 (
    .addr(Address), .din(WriteData), .data(Data_Read), .str(MemWrite), .clk(not_1_out), .ld(MemRead),
    .clr(CLear));  // open: sel
endmodule

module Instruction (
  input  [7:0] PC_Write,
  input  Clock,
  input  Reset,
  output [7:0] PC_Read,
  output [15:0] PC_out
);

  Register #(.trigger("falling")) PC (.D(PC_Write), .Q(PC_Read), .clk(Clock), .clr(Reset));  // open: en
  ROM #(.dataWidth(16)) rom_1 (.addr(PC_Read), .data(PC_out), .sel(1'b1));

  // Notes on the sheet:
  //   contents of rom_1 (hex, n*v repeats v):
  //   3013 1000 1000 8112 1000 4120 314 1000 1000 f422 1000 7111 2244 1000 5125 c120 1000 6015 d205
endmodule

module Control (
  input  [3:0] OP_Code,
  output [11:0] Control_Signals
);

  ROM #(.addrWidth(4), .dataWidth(12)) rom_1 (.addr(OP_Code), .data(Control_Signals));  // open: sel

  // Notes on the sheet:
  //   contents of rom_1 (hex, n*v repeats v):
  //   901 505 440 500 780 902 503 501 900 903 11 506 8 904 502 21
endmodule

module instruction_decode (
  input  [15:0] instruction,
  output [7:0] jump_addr,
  output stall,
  output [3:0] _12_15,
  output [3:0] _8_11,
  output [3:0] _4_7,
  output [3:0] _0_3
);

  wire comparator_1_eq;

  Comparator #(.width(16)) comparator_1 (.a({16{1'b1}}), .b(instruction), .eq(comparator_1_eq));  // open: gt, lt
  not not_1 (stall, comparator_1_eq);

  assign _0_3 = instruction[3:0];
  assign _4_7 = instruction[7:4];
  assign _8_11 = instruction[11:8];
  assign _12_15 = instruction[15:12];
  assign jump_addr = instruction[11:4];
endmodule

module _5bitMemory (
  input  MemRead,
  input  MemWrite,
  input  [4:0] Address,
  input  [3:0] WriteData,
  input  CLK,
  input  CLear,
  output [3:0] Data_Read
);

  wire not_1_out;

  not not_1 (not_1_out, CLK);
  RAM #(.addrWidth(5), .dataWidth(4), .bus("separate")) ram_1 (
    .addr(Address), .din(WriteData), .data(Data_Read), .str(MemWrite), .clk(not_1_out), .ld(MemRead),
    .clr(CLear));  // open: sel
endmodule

module address_maker (
  input  [3:0] address_in,
  input  [3:0] registor,
  output [4:0] address_out
);

  wire comparator_1_eq;
  wire [4:0] adder_1_out;

  Comparator #(.width(4), .mode("unsigned")) comparator_1 (
    .a(registor), .b(4'b0110), .eq(comparator_1_eq));  // open: gt, lt
  Adder #(.width(5)) adder_1 (.a({1'b0, address_in}), .b(5'b10000), .out(adder_1_out), .cin(1'b0));  // open: cout
  Multiplexer #(.width(5), .disabled(0), .enable("false")) multiplexer_1 (
    .in0({1'b0, address_in}), .in1(adder_1_out), .out(address_out), .sel(comparator_1_eq));
endmodule
