// Logisim project fix_zarifmahir_V2.circ as structural Verilog: 12 circuits, main circuit FPA
module FPA (
  input  [15:0] Input_A,
  input  [15:0] Input_B,
  output Overflow,
  output Underflow,
  output [15:0] Output
);

  wire Add16_out_sign, Add16_x, InputHandler_larger_s_sign, InputHandler_smaller_s_sign,
       Normalizer_2_overflow, Normalizer_overflow, Rounder_cout;
  wire [4:0] InputHandler_larger_exponent, Normalizer_2_exponent_2, Normalizer_exponent_2,
       OverflowHandler_exponent_2;
  wire [15:0] Add16_sum, InputHandler_larger_s_significand, InputHandler_smaller_s_shifted_significand,
       Normalizer_2_significand, Normalizer_significand, OverflowHandler_significand_2, Rounder_significand_2;

  InputHandler InputHandler (
    .Input_A(Input_A), .Input_B(Input_B), .Smaller_s_Sign(InputHandler_smaller_s_sign),
    .Larger_s_Sign(InputHandler_larger_s_sign), .Larger_Exponent(InputHandler_larger_exponent),
    .Larger_s_Significand(InputHandler_larger_s_significand),
    .Smaller_s_Shifted_Significand(InputHandler_smaller_s_shifted_significand));
  Add16 Add16 (
    .A(InputHandler_larger_s_significand), .B(InputHandler_smaller_s_shifted_significand),
    .Sign_A(InputHandler_larger_s_sign), .Sign_B(InputHandler_smaller_s_sign), .X(Add16_x), .Sum(Add16_sum),
    .Out_Sign(Add16_out_sign));
  Normalizer Normalizer (
    .X(Add16_x), .Sum(Add16_sum), .Exponent(InputHandler_larger_exponent), .Overflow(Normalizer_overflow),
    .Exponent_2(Normalizer_exponent_2), .Significand(Normalizer_significand));  // open: Underflow
  Rounder Rounder (.Significand(Normalizer_significand), .Significand_2(Rounder_significand_2), .Cout(Rounder_cout));
  Normalizer Normalizer_2 (
    .X(Rounder_cout), .Sum(Rounder_significand_2), .Exponent(Normalizer_exponent_2),
    .Overflow(Normalizer_2_overflow), .Underflow(Underflow), .Exponent_2(Normalizer_2_exponent_2),
    .Significand(Normalizer_2_significand));
  or or_1 (Overflow, Normalizer_overflow, Normalizer_2_overflow);
  OverflowHandler OverflowHandler (
    .Exponent(Normalizer_2_exponent_2), .Significand(Normalizer_2_significand), .Overflow(Overflow),
    .Exponent_2(OverflowHandler_exponent_2), .Significand_2(OverflowHandler_significand_2));
  OutputProcessor OutputProc (
    .Sign(Add16_out_sign), .Exponent(OverflowHandler_exponent_2),
    .Significand(OverflowHandler_significand_2), .Output(Output));
endmodule

module InputHandler (
  input  [15:0] Input_A,
  input  [15:0] Input_B,
  output [15:0] Larger_s_Significand,
  output [15:0] Smaller_s_Shifted_Significand,
  output [4:0] Larger_Exponent,
  output Smaller_s_Sign,
  output Larger_s_Sign
);

  wire ExpDiff_ea___eb, InpProc_2_sign, InpProc_sign;
  wire [4:0] ExpDiff_ea___eb_2, InpProc_2_exponent, InpProc_exponent;
  wire [15:0] InpProc_2_significand, InpProc_significand, multiplexer_2_out, shifter_1_out;

  InputProcessor InpProc (
    .Input(Input_A), .Significand(InpProc_significand), .Exponent(InpProc_exponent), .Sign(InpProc_sign));
  InputProcessor InpProc_2 (
    .Input(Input_B), .Significand(InpProc_2_significand), .Exponent(InpProc_2_exponent), .Sign(InpProc_2_sign));
  ExponentialDifference ExpDiff (
    .Exponent_A(InpProc_exponent), .Exponent_B(InpProc_2_exponent), .Sign_A(InpProc_sign),
    .Sign_B(InpProc_2_sign), .Ea___Eb(ExpDiff_ea___eb), .Ea___Eb_2(ExpDiff_ea___eb_2),
    .MAX_Ea__Eb(Larger_Exponent), .Max_s_Sign(Larger_s_Sign), .Min_s_Sign(Smaller_s_Sign));
  Multiplexer #(.width(16)) multiplexer_1 (
    .in0(InpProc_2_significand), .in1(InpProc_significand), .out(Larger_s_Significand),
    .sel(ExpDiff_ea___eb), .en(1'b1));
  Multiplexer #(.width(16)) multiplexer_2 (
    .in0(InpProc_significand), .in1(InpProc_2_significand), .out(multiplexer_2_out), .sel(ExpDiff_ea___eb),
    .en(1'b1));
  Shifter #(.width(16), .shift("lr")) shifter_1 (
    .in(multiplexer_2_out), .\dist (ExpDiff_ea___eb_2[3:0]), .out(shifter_1_out));
  Multiplexer #(.width(16)) multiplexer_3 (
    .in0(shifter_1_out), .in1({16{1'b0}}), .out(Smaller_s_Shifted_Significand), .sel(ExpDiff_ea___eb_2[4]),
    .en(1'b1));
endmodule

module InputProcessor (
  input  [15:0] Input,
  output [15:0] Significand,
  output [4:0] Exponent,
  output Sign
);

  _10to16 _10to16 (.Fraction(Input[9:0]), .Significand(Significand));

  assign Exponent = Input[14:10];
  assign Sign = Input[15];
endmodule

module _10to16 (
  input  [9:0] Fraction,
  output [15:0] Significand
);


  assign Significand = {1'b1, Fraction, {5{1'b0}}};
endmodule

module ExponentialDifference (
  input  [4:0] Exponent_A,
  input  [4:0] Exponent_B,
  input  Sign_A,
  input  Sign_B,
  output Ea___Eb,
  output [4:0] Ea___Eb_2,
  output [4:0] MAX_Ea__Eb,
  output Max_s_Sign,
  output Min_s_Sign
);

  wire [4:0] multiplexer_2_out;

  Comparator #(.width(5), .mode("unsigned")) comparator_1 (
    .a(Exponent_A), .b(Exponent_B), .gt(Ea___Eb));  // open: eq, lt
  Multiplexer #(.width(5)) multiplexer_1 (
    .in0(Exponent_B), .in1(Exponent_A), .out(MAX_Ea__Eb), .sel(Ea___Eb), .en(1'b1));
  Multiplexer #(.width(5)) multiplexer_2 (
    .in0(Exponent_A), .in1(Exponent_B), .out(multiplexer_2_out), .sel(Ea___Eb), .en(1'b1));
  Multiplexer multiplexer_3 (.in0(Sign_B), .in1(Sign_A), .out(Max_s_Sign), .sel(Ea___Eb), .en(1'b1));
  Multiplexer multiplexer_4 (.in0(Sign_A), .in1(Sign_B), .out(Min_s_Sign), .sel(Ea___Eb), .en(1'b1));
  Subtractor #(.width(5)) subtractor_1 (
    .a(MAX_Ea__Eb), .b(multiplexer_2_out), .out(Ea___Eb_2), .bin(1'b0));  // open: bout
endmodule

module Add16 (
  input  [15:0] A,
  input  [15:0] B,
  input  Sign_A,
  input  Sign_B,
  output X,
  output [15:0] Sum,
  output Out_Sign
);

  wire adder_1_cout, and_2_out, comparator_1_eq, comparator_1_lt, multiplexer_1_out, not_1_out, xor_1_out;
  wire [15:0] adder_1_out, multiplexer_2_out, negator_1_out, subtractor_1_out;

  Adder #(.width(16)) adder_1 (.a(A), .b(B), .out(adder_1_out), .cin(1'b0), .cout(adder_1_cout));
  Subtractor #(.width(16)) subtractor_1 (.a(A), .b(B), .out(subtractor_1_out), .bin(1'b0));  // open: bout
  Comparator #(.width(16), .mode("unsigned")) comparator_1 (
    .a(A), .b(B), .eq(comparator_1_eq), .lt(comparator_1_lt));  // open: gt
  xor xor_1 (xor_1_out, Sign_A, Sign_B);
  Negator #(.width(16)) negator_1 (.in(subtractor_1_out), .out(negator_1_out));
  Multiplexer #(.enable("false")) multiplexer_1 (
    .in0(Sign_A), .in1(Sign_B), .out(multiplexer_1_out), .sel(comparator_1_lt));
  Multiplexer #(.width(16), .enable("false")) multiplexer_2 (
    .in0(subtractor_1_out), .in1(negator_1_out), .out(multiplexer_2_out), .sel(comparator_1_lt));
  not not_1 (not_1_out, xor_1_out);
  Multiplexer #(.width(16), .enable("false")) multiplexer_3 (
    .in0(adder_1_out), .in1(multiplexer_2_out), .out(Sum), .sel(xor_1_out));
  Multiplexer #(.enable("false")) multiplexer_4 (.in0(multiplexer_1_out), .in1(1'b0), .out(Out_Sign), .sel(and_2_out));
  and and_1 (X, adder_1_cout, not_1_out);
  and and_2 (and_2_out, comparator_1_eq, xor_1_out);
endmodule

module Normalizer (
  input  X,
  input  [15:0] Sum,
  input  [4:0] Exponent,
  output Overflow,
  output Underflow,
  output [4:0] Exponent_2,
  output [15:0] Significand
);

  wire and_1_out, comparator_1_gt, ExpAddSub_overflow, not_1_out, not_2_out, priority_encoder_1_en_out;
  wire [3:0] multiplexer_1_out, multiplexer_2_out, priority_encoder_1_out, subtractor_1_out;
  wire [4:0] ExpAddSub_exponent_result, subtractor_2_out;
  wire [4:4] multiplexer_2_out_2;
  wire [15:0] Normalizer_Helper_significand;

  not not_1 (not_1_out, X);
  Priority_Encoder #(.select(4)) priority_encoder_1 (
    .in0(Sum[0]), .in1(Sum[1]), .in2(Sum[2]), .in3(Sum[3]), .in4(Sum[4]), .in5(Sum[5]), .in6(Sum[6]),
    .in7(Sum[7]), .in8(Sum[8]), .in9(Sum[9]), .in10(Sum[10]), .in11(Sum[11]), .in12(Sum[12]), .in13(Sum[13]),
    .in14(Sum[14]), .in15(Sum[15]), .out(priority_encoder_1_out), .en_out(priority_encoder_1_en_out),
    .en_in(1'b1));  // open: gs
  NormHelper Normalizer_Helper (
    .Cout(X), .Sum(Sum), .Shift(multiplexer_1_out), .nX(not_1_out),
    .Significand(Normalizer_Helper_significand));
  and and_1 (and_1_out, not_1_out, priority_encoder_1_en_out);
  Subtractor #(.width(4)) subtractor_1 (
    .a(4'b1111), .b(priority_encoder_1_out), .out(subtractor_1_out), .bin(1'b0));  // open: bout
  Subtractor #(.width(5)) subtractor_2 (.a(Exponent), .b(5'b00001), .out(subtractor_2_out), .bin(1'b0));  // open: bout
  Multiplexer #(.width(4), .enable("false")) multiplexer_1 (
    .in0(4'b0001), .in1(multiplexer_2_out), .out(multiplexer_1_out), .sel(not_1_out));
  ExpAddSub ExpAddSub (
    .Exponent(Exponent), .Shift(multiplexer_1_out), .nX(not_1_out), .Overflow(ExpAddSub_overflow),
    .Exponent_Result(ExpAddSub_exponent_result));  // open: Underflow
  not not_2 (not_2_out, Normalizer_Helper_significand[15]);
  Comparator #(.width(5), .mode("unsigned")) comparator_1 (
    .a({1'b0, subtractor_1_out}), .b(subtractor_2_out), .gt(comparator_1_gt));  // open: eq, lt
  Multiplexer #(.width(5), .enable("false")) multiplexer_2 (
    .in0({1'b0, subtractor_1_out}), .in1(subtractor_2_out),
    .out({multiplexer_2_out_2[4], multiplexer_2_out}), .sel(comparator_1_gt));
  Multiplexer #(.enable("false")) multiplexer_3 (.in0(ExpAddSub_overflow), .in1(1'b0), .out(Overflow), .sel(and_1_out));
  Multiplexer #(.enable("false")) multiplexer_4 (.in0(not_2_out), .in1(1'b0), .out(Underflow), .sel(and_1_out));
  Multiplexer #(.width(5), .enable("false")) multiplexer_5 (
    .in0(ExpAddSub_exponent_result), .in1({5{1'b0}}), .out(Exponent_2), .sel(and_1_out));
  Multiplexer #(.width(16), .enable("false")) multiplexer_6 (
    .in0(Normalizer_Helper_significand), .in1({16{1'b0}}), .out(Significand), .sel(and_1_out));
endmodule

module NormHelper (
  input  Cout,
  input  [15:0] Sum,
  input  [3:0] Shift,
  input  nX,
  output [15:0] Significand
);

  wire [15:0] shifter_1_out;

  Shifter #(.width(16)) shifter_1 (.in(Sum), .\dist (Shift), .out(shifter_1_out));
  Multiplexer #(.width(16), .enable("false")) multiplexer_1 (
    .in0({Cout, Sum[15:1]}), .in1(shifter_1_out), .out(Significand), .sel(nX));
endmodule

module ExpAddSub (
  input  [4:0] Exponent,
  input  [3:0] Shift,
  input  nX,
  output Overflow,
  output Underflow,
  output [4:0] Exponent_Result
);

  wire adder_1_cout, and_1_out, nor_1_out, not_1_out, or_1_out, or_2_out, subtractor_1_bout;
  wire [4:0] adder_1_out, subtractor_1_out;

  Adder #(.width(5)) adder_1 (.a(Exponent), .b({1'b0, Shift}), .out(adder_1_out), .cin(1'b0), .cout(adder_1_cout));
  Subtractor #(.width(5)) subtractor_1 (
    .a(Exponent), .b({1'b0, Shift}), .out(subtractor_1_out), .bin(1'b0), .bout(subtractor_1_bout));
  Multiplexer #(.width(5), .enable("false")) multiplexer_1 (
    .in0(adder_1_out), .in1(subtractor_1_out), .out(Exponent_Result), .sel(nX));
  not not_1 (not_1_out, nX);
  and and_1 (and_1_out, Exponent_Result[0], Exponent_Result[1], Exponent_Result[2], Exponent_Result[3], Exponent_Result[4]);
  nor nor_1 (nor_1_out, Exponent_Result[0], Exponent_Result[1], Exponent_Result[2], Exponent_Result[3], Exponent_Result[4]);
  or or_1 (or_1_out, adder_1_cout, and_1_out);
  or or_2 (or_2_out, nor_1_out, subtractor_1_bout);
  and and_2 (Overflow, not_1_out, or_1_out);
  and and_3 (Underflow, or_2_out, nX);
endmodule

module Rounder (
  input  [15:0] Significand,
  output [15:0] Significand_2,
  output Cout
);

  wire and_1_out, or_1_out, or_2_out;

  or or_1 (or_1_out, Significand[0], Significand[1], Significand[2]);
  or or_2 (or_2_out, or_1_out, Significand[3], Significand[5]);
  and and_1 (and_1_out, or_2_out, Significand[4]);
  Adder #(.width(11)) adder_1 (
    .a(Significand[15:5]), .b({11{1'b0}}), .out(Significand_2[15:5]), .cin(and_1_out), .cout(Cout));

  assign Significand_2[4:0] = {5{1'b0}};
endmodule

module OutputProcessor (
  input  Sign,
  input  [4:0] Exponent,
  input  [15:0] Significand,
  output [15:0] Output
);

  Multiplexer #(.width(5), .enable("false")) multiplexer_1 (
    .in0({5{1'b0}}), .in1(Exponent), .out(Output[14:10]), .sel(Significand[15]));

  assign {Output[15], Output[9:0]} = {Sign, Significand[14:5]};
endmodule

module OverflowHandler (
  input  Overflow,
  input  [4:0] Exponent,
  input  [15:0] Significand,
  output [4:0] Exponent_2,
  output [15:0] Significand_2
);

  Multiplexer #(.width(5), .enable("false")) multiplexer_1 (
    .in0(Exponent), .in1(5'b00001), .out(Exponent_2), .sel(Overflow));
  Multiplexer #(.width(16), .enable("false")) multiplexer_2 (
    .in0(Significand), .in1(16'h8000), .out(Significand_2), .sel(Overflow));
endmodule
