// Logisim project FPA.circ as structural Verilog: 12 circuits, main circuit FPA
module Add16 (
  input  sign_A,
  input  [15:0] A,
  input  sign_B,
  input  [15:0] B,
  output X,
  output [15:0] Sum,
  output Out_Sign
);

  wire adder_1_cout, comparator_1_eq, comparator_1_lt, multiplexer_3_out, multiplexer_4_out, not_1_out,
       xor_1_out;
  wire [15:0] adder_1_out, multiplexer_1_out, negator_1_out, subtractor_1_out;

  xor xor_1 (xor_1_out, sign_A, sign_B);
  Adder #(.width(16)) adder_1 (.a(A), .b(B), .out(adder_1_out), .cin(1'b0), .cout(adder_1_cout));
  Subtractor #(.width(16)) subtractor_1 (.a(A), .b(B), .out(subtractor_1_out), .bin(1'b0));  // open: bout
  Comparator #(.width(16), .mode("unsigned")) comparator_1 (
    .a(A), .b(B), .eq(comparator_1_eq), .lt(comparator_1_lt));  // open: gt
  Negator #(.width(16)) negator_1 (.in(subtractor_1_out), .out(negator_1_out));
  Multiplexer #(.width(16), .disabled(0), .enable("false")) multiplexer_1 (
    .in0(subtractor_1_out), .in1(negator_1_out), .out(multiplexer_1_out), .sel(comparator_1_lt));
  Multiplexer #(.width(16), .disabled(0), .enable("false")) multiplexer_2 (
    .in0(adder_1_out), .in1(multiplexer_1_out), .out(Sum), .sel(xor_1_out));
  not not_1 (not_1_out, xor_1_out);
  and and_1 (X, not_1_out, adder_1_cout);
  Multiplexer #(.disabled(0), .enable("false")) multiplexer_3 (
    .in0(sign_A), .in1(sign_B), .out(multiplexer_3_out), .sel(comparator_1_lt));
  Multiplexer #(.disabled(0), .enable("false")) multiplexer_4 (
    .in0(multiplexer_3_out), .in1(1'b0), .out(multiplexer_4_out), .sel(comparator_1_eq));
  Multiplexer #(.disabled(0), .enable("false")) multiplexer_5 (
    .in0(sign_A), .in1(multiplexer_4_out), .out(Out_Sign), .sel(xor_1_out));
endmodule

module _11to16 (
  input  [10:0] in_1,
  output [15:0] out_2
);


  assign out_2 = {1'b1, in_1, 4'b0000};
endmodule

module ExpDiff (
  input  [3:0] Ea,
  input  [3:0] Eb,
  input  Sa,
  input  Sb,
  output Ea___Eb,
  output [3:0] Ea___Eb_2,
  output [3:0] max_Ea__Eb,
  output Max_sign,
  output Min_sign
);

  wire [3:0] multiplexer_1_out;
  wire [4:4] subtractor_1_out;

  Comparator #(.width(4), .mode("unsigned")) comparator_1 (.a(Ea), .b(Eb), .gt(Ea___Eb));  // open: eq, lt
  Multiplexer #(.width(4), .disabled(0)) multiplexer_1 (
    .in0(Ea), .in1(Eb), .out(multiplexer_1_out), .sel(Ea___Eb), .en(1'b1));
  Multiplexer #(.width(4), .disabled(0)) multiplexer_2 (.in0(Eb), .in1(Ea), .out(max_Ea__Eb), .sel(Ea___Eb), .en(1'b1));
  Subtractor #(.width(5)) subtractor_1 (
    .a({1'b0, max_Ea__Eb}), .b({1'b0, multiplexer_1_out}), .out({subtractor_1_out[4], Ea___Eb_2}), .bin(1'b0));  // open: bout
  Multiplexer #(.disabled(0)) multiplexer_3 (.in0(Sb), .in1(Sa), .out(Max_sign), .sel(Ea___Eb), .en(1'b1));
  Multiplexer #(.disabled(0)) multiplexer_4 (.in0(Sa), .in1(Sb), .out(Min_sign), .sel(Ea___Eb), .en(1'b1));
endmodule

module InpProc (
  input  [15:0] Input,
  output Sign,
  output [3:0] Exponent,
  output [15:0] Significand
);

  _11to16 u_11to16_1 (.in_1(Input[10:0]), .out_2(Significand));

  assign Exponent = Input[14:11];
  assign Sign = Input[15];
endmodule

module InpHand (
  input  [15:0] A,
  input  [15:0] B,
  output [15:0] larger_s_significand,
  output [15:0] smaller_s_shifted_significand,
  output [15:0] smaller_s_significand,
  output [3:0] larger_s_exp,
  output [3:0] exp_diff,
  output smaller_s_sign,
  output larger_s_sign
);

  wire ExpDiff_ea___eb, InpProc_2_sign, InpProc_sign;
  wire [3:0] InpProc_2_exponent, InpProc_exponent;
  wire [15:0] InpProc_2_significand, InpProc_significand;

  InpProc InpProc (.Input(A), .Sign(InpProc_sign), .Exponent(InpProc_exponent), .Significand(InpProc_significand));
  InpProc InpProc_2 (
    .Input(B), .Sign(InpProc_2_sign), .Exponent(InpProc_2_exponent), .Significand(InpProc_2_significand));
  ExpDiff ExpDiff (
    .Ea(InpProc_exponent), .Eb(InpProc_2_exponent), .Sa(InpProc_sign), .Sb(InpProc_2_sign),
    .Ea___Eb(ExpDiff_ea___eb), .Ea___Eb_2(exp_diff), .max_Ea__Eb(larger_s_exp), .Max_sign(larger_s_sign),
    .Min_sign(smaller_s_sign));
  Multiplexer #(.width(16)) multiplexer_1 (
    .in0(InpProc_2_significand), .in1(InpProc_significand), .out(larger_s_significand),
    .sel(ExpDiff_ea___eb), .en(1'b1));
  Multiplexer #(.width(16)) multiplexer_2 (
    .in0(InpProc_significand), .in1(InpProc_2_significand), .out(smaller_s_significand),
    .sel(ExpDiff_ea___eb), .en(1'b1));
  ARS ars_1 (.Input(smaller_s_significand), .Shift_amount(exp_diff), .Output(smaller_s_shifted_significand));
endmodule

module ExpAddSub (
  input  [3:0] Exp,
  input  [3:0] x,
  input  S,
  output Overflow,
  output [3:0] Sum,
  output Underflow
);

  wire adder_1_cout, and_1_out, nor_1_out, not_1_out, or_1_out, or_2_out, subtractor_1_bout;
  wire [3:0] adder_1_out, subtractor_1_out;

  Adder #(.width(4)) adder_1 (.a(Exp), .b(x), .out(adder_1_out), .cout(adder_1_cout));  // open: cin
  Subtractor #(.width(4)) subtractor_1 (.a(Exp), .b(x), .out(subtractor_1_out), .bout(subtractor_1_bout));  // open: bin
  Multiplexer #(.width(4)) multiplexer_1 (.in0(adder_1_out), .in1(subtractor_1_out), .out(Sum), .sel(S), .en(1'b1));
  not not_1 (not_1_out, S);
  and and_1 (and_1_out, Sum[0], Sum[1], Sum[2], Sum[3]);
  nor nor_1 (nor_1_out, Sum[0], Sum[1], Sum[2], Sum[3]);
  or or_1 (or_1_out, adder_1_cout, and_1_out);
  or or_2 (or_2_out, nor_1_out, subtractor_1_bout);
  and and_2 (Overflow, not_1_out, or_1_out);
  and and_3 (Underflow, or_2_out, S);
endmodule

// Helper
module NormHelper (
  input  Cout,
  input  [15:0] Sum,
  input  [3:0] Shift,
  input  S,
  output [15:0] Significand
);

  wire [15:0] als_1_output;

  ALS als_1 (.Input(Sum), .Shift_Amount(Shift), .Output(als_1_output));
  Multiplexer #(.width(16), .disabled(0), .enable("false")) multiplexer_1 (
    .in0({Cout, Sum[15:1]}), .in1(als_1_output), .out(Significand), .sel(S));
endmodule

module Rounder (
  input  [15:0] Significand,
  output Cout,
  output [15:0] Significand_2
);

  wire and_1_out, or_1_out, or_2_out;

  or or_1 (or_1_out, Significand[0], Significand[1]);
  or or_2 (or_2_out, or_1_out, Significand[2], Significand[4]);
  and and_1 (and_1_out, or_2_out, Significand[3]);
  Adder #(.width(12)) adder_1 (
    .a(Significand[15:4]), .b({12{1'b0}}), .out(Significand_2[15:4]), .cin(and_1_out), .cout(Cout));

  assign Significand_2[3:0] = 4'b0000;
endmodule

module OutProc (
  input  Sign,
  input  [3:0] Exponent,
  input  [15:0] Significand,
  output [15:0] Output
);


  assign Output = {Sign, Exponent, Significand[14:4]};
endmodule

module FPA (
  input  [15:0] Input_A,
  input  [15:0] Input_B,
  output Overflow,
  output Underflow,
  output [15:0] Output
);

  wire Add16_out_sign, Add16_x, InpHand_larger_s_sign, InpHand_smaller_s_sign, Rnd_cout;
  wire [3:0] InpHand_larger_s_exp, Norm_exponent_2, Normalizer_exponent_2;
  wire [15:0] Add16_sum, InpHand_larger_s_significand, InpHand_smaller_s_shifted_significand,
       Norm_significand, Normalizer_significand, Rnd_significand_2;

  InpHand InpHand (
    .A(Input_A), .B(Input_B), .larger_s_exp(InpHand_larger_s_exp), .smaller_s_sign(InpHand_smaller_s_sign),
    .larger_s_sign(InpHand_larger_s_sign), .larger_s_significand(InpHand_larger_s_significand),
    .smaller_s_shifted_significand(InpHand_smaller_s_shifted_significand));  // open: exp_diff, smaller_s_significand
  Add16 Add16 (
    .sign_A(InpHand_larger_s_sign), .A(InpHand_larger_s_significand), .sign_B(InpHand_smaller_s_sign),
    .B(InpHand_smaller_s_shifted_significand), .X(Add16_x), .Sum(Add16_sum), .Out_Sign(Add16_out_sign));
  Normalizer Norm (
    .X(Add16_x), .Sum(Add16_sum), .Exponent(InpHand_larger_s_exp), .Overflow(Overflow),
    .Underflow(Underflow), .Exponent_2(Norm_exponent_2), .Significand(Norm_significand));
  Rounder Rnd (.Significand(Norm_significand), .Cout(Rnd_cout), .Significand_2(Rnd_significand_2));
  Normalizer Normalizer (
    .X(Rnd_cout), .Sum(Rnd_significand_2), .Exponent(Norm_exponent_2), .Exponent_2(Normalizer_exponent_2),
    .Significand(Normalizer_significand));  // open: Overflow, Underflow
  OutProc OutProc (
    .Sign(Add16_out_sign), .Exponent(Normalizer_exponent_2), .Significand(Normalizer_significand),
    .Output(Output));
endmodule

module Normalizer (
  input  X,
  input  [15:0] Sum,
  input  [3:0] Exponent,
  output Overflow,
  output Underflow,
  output [3:0] Exponent_2,
  output [15:0] Significand
);

  wire and_1_out, ExpAddSub_overflow, ExpAddSub_underflow, not_1_out, priority_encoder_1_en_out;
  wire [3:0] ExpAddSub_sum, multiplexer_1_out, priority_encoder_1_out, subtractor_1_out;
  wire [15:0] normhelper_1_significand;

  not not_1 (not_1_out, X);
  Priority_Encoder #(.select(4)) priority_encoder_1 (
    .in0(Sum[0]), .in1(Sum[1]), .in2(Sum[2]), .in3(Sum[3]), .in4(Sum[4]), .in5(Sum[5]), .in6(Sum[6]),
    .in7(Sum[7]), .in8(Sum[8]), .in9(Sum[9]), .in10(Sum[10]), .in11(Sum[11]), .in12(Sum[12]), .in13(Sum[13]),
    .in14(Sum[14]), .in15(Sum[15]), .out(priority_encoder_1_out), .en_out(priority_encoder_1_en_out),
    .en_in(1'b1));  // open: gs
  and and_1 (and_1_out, not_1_out, priority_encoder_1_en_out);
  NormHelper normhelper_1 (
    .Cout(X), .Sum(Sum), .Shift(multiplexer_1_out), .S(not_1_out), .Significand(normhelper_1_significand));
  Subtractor #(.width(4)) subtractor_1 (
    .a(4'b1111), .b(priority_encoder_1_out), .out(subtractor_1_out), .bin(1'b0));  // open: bout
  Multiplexer #(.width(4), .disabled(0), .enable("false")) multiplexer_1 (
    .in0(4'b0001), .in1(subtractor_1_out), .out(multiplexer_1_out), .sel(not_1_out));
  ExpAddSub ExpAddSub (
    .Exp(Exponent), .x(multiplexer_1_out), .S(not_1_out), .Overflow(ExpAddSub_overflow), .Sum(ExpAddSub_sum),
    .Underflow(ExpAddSub_underflow));
  Multiplexer #(.disabled(0), .enable("false")) multiplexer_2 (
    .in0(ExpAddSub_overflow), .in1(1'b0), .out(Overflow), .sel(and_1_out));
  Multiplexer #(.disabled(0), .enable("false")) multiplexer_3 (
    .in0(ExpAddSub_underflow), .in1(1'b0), .out(Underflow), .sel(and_1_out));
  Multiplexer #(.width(4), .disabled(0), .enable("false")) multiplexer_4 (
    .in0(ExpAddSub_sum), .in1(4'b0000), .out(Exponent_2), .sel(and_1_out));
  Multiplexer #(.width(16), .disabled(0), .enable("false")) multiplexer_5 (
    .in0(normhelper_1_significand), .in1({16{1'b0}}), .out(Significand), .sel(and_1_out));
endmodule

module Circuit_Tester_circ (
  input  x,
  input  a0,
  input  a1,
  input  a2,
  input  a3,
  input  a4,
  input  a5,
  input  a6,
  input  a7,
  input  a8,
  input  a9,
  input  a10,
  input  a11,
  input  a12,
  input  a13,
  input  a14,
  input  a15,
  input  b0,
  input  b1,
  input  b2,
  input  b3,
  input  b4,
  input  b5,
  input  b6,
  input  b7,
  input  b8,
  input  b9,
  input  b10,
  input  b11,
  input  b12,
  input  b13,
  input  b14,
  input  b15,
  output x_2,
  output Ov,
  output Un,
  output S0,
  output S1,
  output S2,
  output S3,
  output S4,
  output S5,
  output S6,
  output S7,
  output S8,
  output S9,
  output S10,
  output S11,
  output S12,
  output S13,
  output S14,
  output S15
);

  FPA FPA (
    .Input_A({a15, a14, a13, a12, a11, a10, a9, a8, a7, a6, a5, a4, a3, a2, a1, a0}),
    .Input_B({b15, b14, b13, b12, b11, b10, b9, b8, b7, b6, b5, b4, b3, b2, b1, b0}), .Overflow(Ov),
    .Underflow(Un), .Output({S15, S14, S13, S12, S11, S10, S9, S8, S7, S6, S5, S4, S3, S2, S1, S0}));

  assign x_2 = x;
endmodule
