// Logisim project MIPS_Final.circ as structural Verilog: 14 circuits, main circuit 4-bit ALU
// ALU
module _4_bit_ALU (
  input  [3:0] A,
  input  [2:0] ALUSel,
  input  [3:0] B,
  output [3:0] Output,
  output Zero_Flag
);

  wire [3:0] adder_1_out, and_1_out, nor_1_out, or_1_out, shifter_1_out, shifter_2_out, subtractor_1_out;

  Adder #(.width(4)) adder_1 (.a(A), .b(B), .out(adder_1_out), .cin(1'b0));  // open: cout
  Subtractor #(.width(4)) subtractor_1 (.a(A), .b(B), .out(subtractor_1_out), .bin(1'b0));  // open: bout
  assign and_1_out = A & B;  // AND_Gate and_1, 4 bits wide
  assign or_1_out = A | B;  // OR_Gate or_1, 4 bits wide
  assign nor_1_out = ~(A | B);  // NOR_Gate nor_1, 4 bits wide
  Shifter #(.width(4)) shifter_1 (.in(A), .\dist (B[1:0]), .out(shifter_1_out));
  Shifter #(.width(4), .shift("lr")) shifter_2 (.in(A), .\dist (B[1:0]), .out(shifter_2_out));
  Multiplexer #(.select(3), .width(4), .enable("false")) multiplexer_1 (
    .in0(adder_1_out), .in1(subtractor_1_out), .in2(and_1_out), .in3(or_1_out), .in4(nor_1_out),
    .in5(shifter_1_out), .in6(shifter_2_out), .in7(4'b0000), .out(Output), .sel(ALUSel));
  nor nor_2 (Zero_Flag, Output[0], Output[1], Output[2], Output[3]);
endmodule

// Register
module Registers (
  input  RegWrite,
  input  [3:0] WR,
  input  [3:0] WriteData,
  input  CLK,
  input  RST,
  input  [3:0] SrcReg1,
  input  [3:0] SrcReg2,
  output [19:0] t4__t3__t2__t1__t0,
  output [3:0] ReadData1,
  output [3:0] ReadData2
);

  wire demultiplexer_1_out1, demultiplexer_1_out2, demultiplexer_1_out3, demultiplexer_1_out4,
       demultiplexer_1_out5;

  Register #(.width(4), .trigger("falling")) t0 (
    .D(WriteData), .en(demultiplexer_1_out1), .Q(t4__t3__t2__t1__t0[3:0]), .clk(CLK), .clr(RST));
  Multiplexer #(.select(3), .width(4), .enable("false")) multiplexer_1 (
    .in0(4'b0000), .in1(t4__t3__t2__t1__t0[3:0]), .in2(t4__t3__t2__t1__t0[7:4]),
    .in3(t4__t3__t2__t1__t0[11:8]), .in4(t4__t3__t2__t1__t0[15:12]), .in5(t4__t3__t2__t1__t0[19:16]),
    .out(ReadData1), .sel(SrcReg1[2:0]));  // open: in6, in7
  Demultiplexer #(.select(3), .enable("false")) demultiplexer_1 (
    .out1(demultiplexer_1_out1), .out2(demultiplexer_1_out2), .out3(demultiplexer_1_out3),
    .out4(demultiplexer_1_out4), .out5(demultiplexer_1_out5), .in(RegWrite), .sel(WR[2:0]));  // open: out0, out6, out7
  Register #(.width(4), .trigger("falling")) t1 (
    .D(WriteData), .en(demultiplexer_1_out2), .Q(t4__t3__t2__t1__t0[7:4]), .clk(CLK), .clr(RST));
  Register #(.width(4), .trigger("falling")) t2 (
    .D(WriteData), .en(demultiplexer_1_out3), .Q(t4__t3__t2__t1__t0[11:8]), .clk(CLK), .clr(RST));
  Register #(.width(4), .trigger("falling")) t3 (
    .D(WriteData), .en(demultiplexer_1_out4), .Q(t4__t3__t2__t1__t0[15:12]), .clk(CLK), .clr(RST));
  Register #(.width(4), .trigger("falling")) t4 (
    .D(WriteData), .en(demultiplexer_1_out5), .Q(t4__t3__t2__t1__t0[19:16]), .clk(CLK), .clr(RST));
  Multiplexer #(.select(3), .width(4), .enable("false")) multiplexer_2 (
    .in0(4'b0000), .in1(t4__t3__t2__t1__t0[3:0]), .in2(t4__t3__t2__t1__t0[7:4]),
    .in3(t4__t3__t2__t1__t0[11:8]), .in4(t4__t3__t2__t1__t0[15:12]), .in5(t4__t3__t2__t1__t0[19:16]),
    .out(ReadData2), .sel(SrcReg2[2:0]));  // open: in6, in7
endmodule

module Control (
  input  [3:0] Opcode,
  output [11:0] Control_Signals
);

  ROM #(.addrWidth(4), .dataWidth(12)) rom_1 (.addr(Opcode), .data(Control_Signals));  // open: sel

  // Notes on the sheet:
  //   contents of rom_1 (hex, n*v repeats v):
  //   2e 201 31 88 33 101 829 2b 2a 2d 32 68 34 828 30 400
endmodule

module IF_ID (
  input  [15:0] instr_in,
  input  [7:0] pc1_in,
  input  Flush,
  input  En,
  input  RST,
  input  CLK,
  output [15:0] instr,
  output [7:0] pc1_in_2
);

  wire [7:0] multiplexer_1_out;
  wire [15:0] multiplexer_2_out;

  Multiplexer #(.width(8)) multiplexer_1 (
    .in0(pc1_in), .in1({8{1'b0}}), .out(multiplexer_1_out), .sel(Flush));  // open: en
  Register register_1 (.D(multiplexer_1_out), .en(En), .Q(pc1_in_2), .clk(CLK), .clr(RST));
  Multiplexer #(.width(16)) multiplexer_2 (
    .in0(instr_in), .in1({16{1'b0}}), .out(multiplexer_2_out), .sel(Flush));  // open: en
  Register #(.width(16)) register_2 (.D(multiplexer_2_out), .en(En), .Q(instr), .clk(CLK), .clr(RST));
endmodule

module ID_EX (
  input  [11:0] ctrl_in,
  input  Bubble,
  input  [7:0] pc1_in,
  input  [3:0] wr_in,
  input  [3:0] rs_in,
  input  [3:0] rt_in,
  input  [3:0] imm_in,
  input  [3:0] rd2_in,
  input  [3:0] rd1_in,
  input  CLK,
  input  RST,
  output [11:0] EX_ctrl,
  output [7:0] Ex_pc1,
  output [3:0] Ex_wr,
  output [3:0] Ex_rs,
  output [3:0] Ex_rt,
  output [3:0] Ex_imm,
  output [3:0] Ex_rd2,
  output [3:0] Ex_rd1
);

  wire [11:0] multiplexer_1_out;

  Multiplexer #(.width(12)) multiplexer_1 (
    .in0(ctrl_in), .in1({12{1'b0}}), .out(multiplexer_1_out), .sel(Bubble));  // open: en
  Register #(.width(12)) ctrl (.D(multiplexer_1_out), .Q(EX_ctrl), .clk(CLK), .clr(RST));  // open: en
  Register register_1 (.D(pc1_in), .Q(Ex_pc1), .clk(CLK), .clr(RST));  // open: en
  Register #(.width(4)) register_2 (.D(wr_in), .Q(Ex_wr), .clk(CLK), .clr(RST));  // open: en
  Register #(.width(4)) register_3 (.D(rs_in), .Q(Ex_rs), .clk(CLK), .clr(RST));  // open: en
  Register #(.width(4)) register_4 (.D(rt_in), .Q(Ex_rt), .clk(CLK), .clr(RST));  // open: en
  Register #(.width(4)) register_5 (.D(imm_in), .Q(Ex_imm), .clk(CLK), .clr(RST));  // open: en
  Register #(.width(4)) register_6 (.D(rd2_in), .Q(Ex_rd2), .clk(CLK), .clr(RST));  // open: en
  Register #(.width(4)) register_7 (.D(rd1_in), .Q(Ex_rd1), .clk(CLK), .clr(RST));  // open: en
endmodule

module EX_MEM (
  input  [11:0] ctrl_in,
  input  [3:0] alu_in,
  input  [3:0] wdata_in,
  input  [7:0] addr_in,
  input  spbase_in,
  input  [3:0] wr_in,
  input  CLK,
  input  RST,
  output [11:0] Mem_ctrl,
  output [3:0] Mem_alu,
  output [3:0] Mem_wdata,
  output [7:0] Mem_addr,
  output Mem_spbase,
  output [3:0] Mem_wr
);

  Register #(.width(12)) register_1 (.D(ctrl_in), .Q(Mem_ctrl), .clk(CLK), .clr(RST));  // open: en
  Register #(.width(4)) register_2 (.D(alu_in), .Q(Mem_alu), .clk(CLK), .clr(RST));  // open: en
  Register #(.width(4)) register_3 (.D(wdata_in), .Q(Mem_wdata), .clk(CLK), .clr(RST));  // open: en
  Register register_4 (.D(addr_in), .Q(Mem_addr), .clk(CLK), .clr(RST));  // open: en
  Register #(.width(1)) register_5 (.D(spbase_in), .Q(Mem_spbase), .clk(CLK), .clr(RST));  // open: en
  Register #(.width(4)) register_6 (.D(wr_in), .Q(Mem_wr), .clk(CLK), .clr(RST));  // open: en
endmodule

module MEM_WB (
  input  [11:0] ctrl_in,
  input  [3:0] alu_in,
  input  [3:0] mdata_in,
  input  [3:0] wr_in,
  input  CLK,
  input  RST,
  output [11:0] WB_ctrl,
  output [3:0] WB_alu,
  output [3:0] WB_mdata,
  output [3:0] WB_wr
);

  Register #(.width(12)) register_1 (.D(ctrl_in), .Q(WB_ctrl), .clk(CLK), .clr(RST));  // open: en
  Register #(.width(4)) register_2 (.D(alu_in), .Q(WB_alu), .clk(CLK), .clr(RST));  // open: en
  Register #(.width(4)) register_3 (.D(mdata_in), .Q(WB_mdata), .clk(CLK), .clr(RST));  // open: en
  Register #(.width(4)) register_4 (.D(wr_in), .Q(WB_wr), .clk(CLK), .clr(RST));  // open: en
endmodule

module IF (
  input  [7:0] Target,
  input  En,
  input  CLK,
  input  Flush,
  input  RST,
  output [7:0] pc,
  output [7:0] pc1
);

  wire [7:0] multiplexer_1_out;

  Register u_PC (.D(multiplexer_1_out), .en(En), .Q(pc), .clk(CLK), .clr(RST));
  Adder adder_1 (.a(pc), .b(8'h1), .out(pc1));  // open: cin, cout
  Multiplexer #(.width(8)) multiplexer_1 (.in0(pc1), .in1(Target), .out(multiplexer_1_out), .sel(Flush));  // open: en
endmodule

module ID (
  input  [15:0] instr,
  input  [3:0] WB_wr,
  input  WB_RegWrite,
  input  [3:0] WB_data,
  input  CLK,
  input  RST,
  input  [3:0] EX_wr,
  input  EX_MemRead,
  output [3:0] rt,
  output [3:0] rs,
  output [3:0] imm,
  output [3:0] wr,
  output [11:0] ctrl,
  output [19:0] t4__t3__t2__t1__t0,
  output [3:0] rd2,
  output [3:0] rd1,
  output stall
);

  Registers registers_1 (
    .WR(WB_wr), .WriteData(WB_data), .CLK(CLK), .RST(RST), .SrcReg1(instr[11:8]), .SrcReg2(instr[7:4]),
    .ReadData1(rd1), .ReadData2(rd2), .RegWrite(WB_RegWrite), .t4__t3__t2__t1__t0(t4__t3__t2__t1__t0));
  Multiplexer #(.width(4)) multiplexer_1 (.in0(instr[7:4]), .in1(instr[3:0]), .out(wr), .sel(ctrl[4]));  // open: en
  Control control_1 (.Opcode(instr[15:12]), .Control_Signals(ctrl));
  hazardUnit hazardunit_1 (
    .EX_wr(EX_wr), .ID_rs(instr[11:8]), .EX_MemRead(EX_MemRead), .ID_rt(instr[7:4]), .Stall(stall));

  assign imm = instr[3:0];
  assign rs = instr[11:8];
  assign rt = instr[7:4];
endmodule

// Hazard
module hazardUnit (
  input  [3:0] EX_wr,
  input  [3:0] ID_rs,
  input  EX_MemRead,
  input  [3:0] ID_rt,
  output Stall
);

  wire comparator_1_eq, comparator_2_eq, or_1_out;

  Comparator #(.width(4)) comparator_1 (.a(EX_wr), .b(ID_rs), .eq(comparator_1_eq));  // open: gt, lt
  Comparator #(.width(4)) comparator_2 (.a(EX_wr), .b(ID_rt), .eq(comparator_2_eq));  // open: gt, lt
  or or_1 (or_1_out, comparator_1_eq, comparator_2_eq);
  and and_1 (Stall, or_1_out, EX_MemRead);
endmodule

module ForwardingUnit (
  input  Mem_RegWrite,
  input  Wb_RegWrite,
  input  [3:0] Mem_wr,
  input  [3:0] Wb_wr,
  input  [3:0] EX_rs,
  input  [3:0] EX_rt,
  output [1:0] ForwardA,
  output [1:0] ForwardB
);

  wire and_2_out, and_4_out, comparator_1_eq, comparator_2_eq, comparator_3_eq, comparator_4_eq,
       comparator_5_eq, comparator_6_eq, not_1_out, not_2_out, not_3_out, not_4_out;

  Comparator #(.width(4)) comparator_1 (.a(Mem_wr), .b(4'b0000), .eq(comparator_1_eq));  // open: gt, lt
  Comparator #(.width(4)) comparator_2 (.a(Wb_wr), .b(4'b0000), .eq(comparator_2_eq));  // open: gt, lt
  Comparator #(.width(4)) comparator_3 (.a(Mem_wr), .b(EX_rs), .eq(comparator_3_eq));  // open: gt, lt
  Comparator #(.width(4)) comparator_4 (.a(Wb_wr), .b(EX_rs), .eq(comparator_4_eq));  // open: gt, lt
  Comparator #(.width(4)) comparator_5 (.a(Mem_wr), .b(EX_rt), .eq(comparator_5_eq));  // open: gt, lt
  Comparator #(.width(4)) comparator_6 (.a(Wb_wr), .b(EX_rt), .eq(comparator_6_eq));  // open: gt, lt
  not not_1 (not_1_out, comparator_1_eq);
  not not_2 (not_2_out, comparator_2_eq);
  and and_1 (ForwardA[1], Mem_RegWrite, not_1_out, comparator_3_eq);
  and and_2 (and_2_out, Wb_RegWrite, not_2_out, comparator_4_eq);
  and and_3 (ForwardB[1], Mem_RegWrite, not_1_out, comparator_5_eq);
  and and_4 (and_4_out, Wb_RegWrite, not_2_out, comparator_6_eq);
  not not_3 (not_3_out, ForwardA[1]);
  not not_4 (not_4_out, ForwardB[1]);
  and and_5 (ForwardA[0], not_3_out, and_2_out);
  and and_6 (ForwardB[0], not_4_out, and_4_out);
endmodule

module EX (
  input  [11:0] ctrl,
  input  Wb_RegWrite,
  input  [3:0] wr,
  input  Mem_RegWrite,
  input  CLK,
  input  [3:0] Mem_wr,
  input  RST,
  input  [3:0] WB_wr,
  input  [3:0] rs,
  input  [7:0] pc1_in,
  input  [3:0] rt,
  input  [3:0] rd1,
  input  [3:0] imm,
  input  [3:0] rd2,
  input  [3:0] Mem_ALU,
  input  [3:0] WB_data,
  output [1:0] ForwardA,
  output [7:0] sp,
  output [1:0] ForwardB,
  output [3:0] Bval,
  output spbase,
  output [7:0] Target,
  output [7:0] addr,
  output [3:0] alu,
  output flush,
  output FWD
);

  wire and_1_out, and_2_out, and_3_out, BrTaken, comparator_2_eq, n4_bit_alu_1_zero_flag, not_1_out;
  wire [3:0] A, multiplexer_3_out;
  wire [7:0] A8, adder_2_out, bit_extender_1_out, brtarget, imm8, multiplexer_5_out, multiplexer_6_out,
       subtractor_1_out;

  Comparator #(.width(4)) comparator_1 (.a(rs), .b(4'b0110), .eq(spbase));  // open: gt, lt
  ForwardingUnit forwardingunit_1 (
    .Mem_wr(Mem_wr), .Wb_wr(WB_wr), .EX_rs(rs), .EX_rt(rt), .Mem_RegWrite(Mem_RegWrite),
    .Wb_RegWrite(Wb_RegWrite), .ForwardA(ForwardA), .ForwardB(ForwardB));
  Multiplexer #(.select(2), .width(4)) multiplexer_1 (
    .in0(rd1), .in1(WB_data), .in2(Mem_ALU), .in3(4'b0000), .out(A), .sel(ForwardA));  // open: en
  Multiplexer #(.select(2), .width(4)) multiplexer_2 (
    .in0(rd2), .in1(WB_data), .in2(Mem_ALU), .in3(4'b0000), .out(Bval), .sel(ForwardB));  // open: en
  Multiplexer #(.width(4)) multiplexer_3 (.in0(Bval), .in1(imm), .out(multiplexer_3_out), .sel(ctrl[3]));  // open: en
  assign bit_extender_1_out = {{4{imm[3]}}, imm};  // Bit_Extender bit_extender_1
  Multiplexer #(.width(8)) multiplexer_4 (.in0(brtarget), .in1({rs, rt}), .out(Target), .sel(ctrl[10]));  // open: en
  Adder adder_1 (.a(pc1_in), .b(bit_extender_1_out), .out(brtarget));  // open: cin, cout
  _4_bit_ALU u_4_bit_alu_1 (
    .A(A), .B(multiplexer_3_out), .ALUSel(ctrl[2:0]), .Output(alu), .Zero_Flag(n4_bit_alu_1_zero_flag));
  not not_1 (not_1_out, n4_bit_alu_1_zero_flag);
  or or_1 (flush, BrTaken, ctrl[10]);
  assign imm8 = {{4{1'b0}}, imm};  // Bit_Extender bit_extender_2
  assign A8 = {{4{1'b0}}, A};  // Bit_Extender bit_extender_3
  and and_1 (and_1_out, ctrl[8], n4_bit_alu_1_zero_flag);
  and and_2 (and_2_out, ctrl[9], not_1_out);
  or or_2 (FWD, ForwardA[0], ForwardA[1], ForwardB[0], ForwardB[1]);
  or or_3 (BrTaken, and_1_out, and_2_out);
  Adder adder_2 (.a(sp), .b(imm8), .out(adder_2_out));  // open: cin, cout
  Subtractor subtractor_1 (.a(sp), .b(imm8), .out(subtractor_1_out));  // open: bin, bout
  Comparator #(.width(4)) comparator_2 (.a(wr), .b(4'b0110), .eq(comparator_2_eq));  // open: gt, lt
  Multiplexer #(.width(8)) multiplexer_5 (.in0(A8), .in1(sp), .out(multiplexer_5_out), .sel(spbase));  // open: en
  and and_3 (and_3_out, comparator_2_eq, ctrl[11]);
  Adder adder_3 (.a(imm8), .b(multiplexer_5_out), .out(addr));  // open: cin, cout
  Multiplexer #(.width(8)) multiplexer_6 (
    .in0(adder_2_out), .in1(subtractor_1_out), .out(multiplexer_6_out), .sel(ctrl[0]));  // open: en
  Register u_sp (.D(multiplexer_6_out), .en(and_3_out), .Q(sp), .clk(CLK), .clr(RST));

  // Other names for the same wires on the sheet: Bv[3:0] = Bval; ALUOP[2:0] = ctrl[2:0]; Subsel = ctrl[0];
  //   ALUSrc = ctrl[3]; Branch = ctrl[8]; BNE = ctrl[9]; Jump = ctrl[10]; ImmArith = ctrl[11]; fA[1:0] = ForwardA;
  //   fB[1:0] = ForwardB; jtarget[7:0] = {rs, rt}; spb = spbase; SPq[7:0] = sp
endmodule

module MEM (
  input  [7:0] addr,
  input  [3:0] wdata,
  input  spbase,
  input  MemWrite,
  input  RST,
  input  CLK,
  output [3:0] mdata
);

  wire and_1_out, and_2_out, not_1_out, not_2_out;
  wire [3:0] ram_1_data, ram_2_data;

  not not_1 (not_1_out, spbase);
  and and_1 (and_1_out, not_1_out, MemWrite);
  and and_2 (and_2_out, spbase, MemWrite);
  RAM #(.dataWidth(4), .bus("separate")) ram_1 (
    .addr(addr), .din(wdata), .data(ram_1_data), .str(and_1_out), .sel(1'b1), .clk(not_2_out), .ld(1'b1),
    .clr(RST));
  RAM #(.dataWidth(4), .bus("separate")) ram_2 (
    .addr(addr), .din(wdata), .data(ram_2_data), .str(and_2_out), .sel(1'b1), .clk(not_2_out), .ld(1'b1),
    .clr(RST));
  not not_2 (not_2_out, CLK);
  Multiplexer #(.width(4), .enable("false")) multiplexer_1 (
    .in0(ram_1_data), .in1(ram_2_data), .out(mdata), .sel(spbase));
endmodule

module Main (
  output [7:0] PC
);

  wire CLK, Ex_Memread, EX_spbase, Flush, FWD, Mem_spbase, not_1_out, or_1_out, RST, Stall;
  wire [1:0] EX_forwarda, EX_forwardb;
  wire [3:0] EX_alu, EX_bval, Ex_wr, ID_EX_ex_imm, ID_EX_ex_rd1, ID_EX_ex_rd2, ID_EX_ex_rs, ID_EX_ex_rt,
       ID_imm, ID_rd1, ID_rd2, ID_rs, ID_rt, ID_t4__t3__t2__t1__t0, ID_t4__t3__t2__t1__t0_2,
       ID_t4__t3__t2__t1__t0_3, ID_t4__t3__t2__t1__t0_4, ID_t4__t3__t2__t1__t0_5, ID_wr, Mem_alu, Mem_mdata,
       Mem_wdata, Mem_wr, WB_alu, WB_data, WB_mdata, WB_wr;
  wire [7:0] EX_addr, EX_sp, Ex_target, ID_EX_ex_pc1, ID_pc1, IF_pc1, Mem_addr;
  wire [11:0] ID_ctrl, ID_EX_ex_ctrl, Mem_ctrl, WB_ctrl;
  wire [15:0] IF_ID_instr, rom_1_data;

  Clock u_CLK (.out(CLK));
  Button u_RST (.out(RST));
  not not_1 (not_1_out, Stall);
  IF IF (.Target(Ex_target), .En(not_1_out), .CLK(CLK), .Flush(Flush), .RST(RST), .pc(PC), .pc1(IF_pc1));
  Hex_Digit_Display hex_digit_display_1 (.value(ID_t4__t3__t2__t1__t0_5));  // open: dp
  LED led_1 (.in(Stall));
  LED led_2 (.in(Flush));
  LED led_3 (.in(FWD));
  Hex_Digit_Display hex_digit_display_2 (.value(ID_t4__t3__t2__t1__t0_3));  // open: dp
  Hex_Digit_Display hex_digit_display_3 (.value(ID_t4__t3__t2__t1__t0_4));  // open: dp
  ROM #(.dataWidth(16)) rom_1 (.addr(PC), .data(rom_1_data), .sel(1'b1));
  Hex_Digit_Display hex_digit_display_4 (.value(ID_t4__t3__t2__t1__t0_2));  // open: dp
  Hex_Digit_Display hex_digit_display_5 (.value(ID_t4__t3__t2__t1__t0));  // open: dp
  IF_ID IF_ID (
    .instr_in(rom_1_data), .pc1_in(IF_pc1), .Flush(Flush), .En(not_1_out), .RST(RST), .CLK(CLK),
    .instr(IF_ID_instr), .pc1_in_2(ID_pc1));
  ID ID (
    .instr(IF_ID_instr), .WB_wr(WB_wr), .WB_data(WB_data), .CLK(CLK), .RST(RST), .EX_wr(Ex_wr),
    .EX_MemRead(Ex_Memread), .rt(ID_rt), .rs(ID_rs), .imm(ID_imm), .wr(ID_wr), .ctrl(ID_ctrl),
    .WB_RegWrite(WB_ctrl[5]),
    .t4__t3__t2__t1__t0({ID_t4__t3__t2__t1__t0_5, ID_t4__t3__t2__t1__t0_4, ID_t4__t3__t2__t1__t0_3, ID_t4__t3__t2__t1__t0_2, ID_t4__t3__t2__t1__t0}),
    .rd2(ID_rd2), .rd1(ID_rd1), .stall(Stall));
  or or_1 (or_1_out, Flush, Stall);
  ID_EX ID_EX (
    .ctrl_in(ID_ctrl), .Bubble(or_1_out), .pc1_in(ID_pc1), .wr_in(ID_wr), .rs_in(ID_rs), .rt_in(ID_rt),
    .imm_in(ID_imm), .rd2_in(ID_rd2), .rd1_in(ID_rd1), .CLK(CLK), .RST(RST),
    .EX_ctrl({ID_EX_ex_ctrl[11:7], Ex_Memread, ID_EX_ex_ctrl[5:0]}), .Ex_pc1(ID_EX_ex_pc1), .Ex_wr(Ex_wr),
    .Ex_rs(ID_EX_ex_rs), .Ex_rt(ID_EX_ex_rt), .Ex_imm(ID_EX_ex_imm), .Ex_rd2(ID_EX_ex_rd2),
    .Ex_rd1(ID_EX_ex_rd1));
  Hex_Digit_Display hex_digit_display_6 (.value(EX_sp[7:4]));  // open: dp
  Hex_Digit_Display hex_digit_display_7 (.value(EX_sp[3:0]));  // open: dp
  EX EX (
    .ctrl({ID_EX_ex_ctrl[11:7], Ex_Memread, ID_EX_ex_ctrl[5:0]}), .wr(Ex_wr), .CLK(CLK), .Mem_wr(Mem_wr),
    .RST(RST), .WB_wr(WB_wr), .rs(ID_EX_ex_rs), .pc1_in(ID_EX_ex_pc1), .rt(ID_EX_ex_rt), .rd1(ID_EX_ex_rd1),
    .imm(ID_EX_ex_imm), .rd2(ID_EX_ex_rd2), .Mem_RegWrite(Mem_ctrl[5]), .Wb_RegWrite(WB_ctrl[5]),
    .Mem_ALU(Mem_alu), .WB_data(WB_data), .ForwardA(EX_forwarda), .sp(EX_sp), .ForwardB(EX_forwardb),
    .Bval(EX_bval), .spbase(EX_spbase), .Target(Ex_target), .addr(EX_addr), .alu(EX_alu), .flush(Flush),
    .FWD(FWD));
  // Probe on EX_forwardb
  // Probe on EX_forwarda
  EX_MEM EX_MEM (
    .ctrl_in({ID_EX_ex_ctrl[11:7], Ex_Memread, ID_EX_ex_ctrl[5:0]}), .alu_in(EX_alu), .wdata_in(EX_bval),
    .addr_in(EX_addr), .spbase_in(EX_spbase), .wr_in(Ex_wr), .CLK(CLK), .RST(RST), .Mem_ctrl(Mem_ctrl),
    .Mem_alu(Mem_alu), .Mem_wdata(Mem_wdata), .Mem_addr(Mem_addr), .Mem_spbase(Mem_spbase), .Mem_wr(Mem_wr));
  MEM MEM (
    .addr(Mem_addr), .wdata(Mem_wdata), .spbase(Mem_spbase), .MemWrite(Mem_ctrl[7]), .CLK(CLK), .RST(RST),
    .mdata(Mem_mdata));
  MEM_WB MEM_WB (
    .ctrl_in(Mem_ctrl), .alu_in(Mem_alu), .mdata_in(Mem_mdata), .wr_in(Mem_wr), .CLK(CLK), .RST(RST),
    .WB_ctrl(WB_ctrl), .WB_alu(WB_alu), .WB_mdata(WB_mdata), .WB_wr(WB_wr));
  Multiplexer #(.width(4)) multiplexer_1 (.in0(WB_alu), .in1(WB_mdata), .out(WB_data), .sel(WB_ctrl[6]));  // open: en

  // Other names for the same wires on the sheet: Mem_regWrite = Mem_ctrl[5]; Mem_MemWrite = Mem_ctrl[7];
  //   WB_regWrite = WB_ctrl[5]; WB_MemRead = WB_ctrl[6]

  // Notes on the sheet:
  //   $t4
  //   $t3
  //   $t2
  //   contents of rom_1 (hex, n*v repeats v):
  //   d015 d023 e123 2324 3242 b252 e555 6661 3610 6661 3620 b631 b640 d661 b610 d661 8526 7228 c203 9341
  //   443 9114 a531 d013 6111 d221 110d 5101 d05f f1f0 d05e f1f0
  //   $t1
  //   $t0
  //   $sp
endmodule
